// Logisim project Pc_8bitCPU.circ as structural Verilog: 21 circuits, main circuit main
module main (
  input  Master_Power,
  input  Reset_SC,
  output T0
);

  wire and_1_out, CLR_out, control_unit_1_pass_acc, control_unit_1_reg_shift__1, decoder_1_out0,
       decoder_1_out1, decoder_1_out2, decoder_1_out3, decoder_2_out0, decoder_2_out1, decoder_2_out2,
       decoder_2_out3, Master_Clear_out, Master_Clock_out, memoryaccess_1_select, memoryaccess_2_select,
       memoryaccess_3_select, memoryaccess_4_select, memoryaccess_5_select, memoryaccess_6_select,
       memoryaccess_7_select, memoryaccess_8_select, memoryaccess_9_select, memoryaccess_10_select,
       memoryaccess_11_select, memoryaccess_12_select, memoryaccess_13_select, memoryaccess_14_select,
       memoryaccess_15_select, memoryaccess_16_select, not_1_out, not_2_out, not_3_out, ram_17_data;
  wire [2:0] control_unit_1_enstsw_m, control_unit_1_s, sipo_shift_reg_1__3bit_out;
  wire [3:0] control_unit_1_lids_8bit, control_unit_1_lids_16bit_2;
  wire [7:0] accumulator_1_a_datain, accumulator_1_alu_input, alu_1_carryout, alu_1_output, ram_1_data,
       regpair_1_busdataout_high, regpair_1_data_high, regpair_1_data_low, regpair_2_data_high,
       regpair_2_data_low, regpair_3_data_high, regpair_3_data_low;
  wire [10:0] control_unit_1_clk_pulses;
  wire [11:0] memoryaccess_1_addressout, memoryaccess_2_addressout, memoryaccess_3_addressout,
       memoryaccess_4_addressout, memoryaccess_5_addressout, memoryaccess_6_addressout,
       memoryaccess_7_addressout, memoryaccess_8_addressout, memoryaccess_9_addressout,
       memoryaccess_10_addressout, memoryaccess_11_addressout, memoryaccess_12_addressout,
       memoryaccess_13_addressout, memoryaccess_14_addressout, memoryaccess_15_addressout,
       memoryaccess_16_addressout;
  wire [15:0] PC_current_value, regpair_1__16bit_out, SP_current_value;
  wire [19:0] control_unit_1_lids_16bit;
  wire [23:0] sipo_shift_reg_1__24bit_out;
  wire [23:4] control_unit_1_lids_8bit_2;

  Button Master_Clear (.out(Master_Clear_out));
  Clock Master_Clock (.out(Master_Clock_out));
  not not_1 (not_1_out, Master_Power);
  not not_2 (not_2_out, 1'b0);
  Accumulator accumulator_1 (
    .ALU_Input(accumulator_1_alu_input), .Bus_Input(regpair_1_busdataout_high), .Bus_to_ACC(and_1_out),
    .ALU_Output(alu_1_output), .ALU_to_ACC(control_unit_1_pass_acc), .A_DataIN(accumulator_1_a_datain),
    .A_DataOUT(regpair_1_data_high));
  ALU alu_1 (
    .A(accumulator_1_alu_input), .B(regpair_1_busdataout_high), .S(control_unit_1_s), .Output(alu_1_output),
    .CarryOUT(alu_1_carryout[0]), .Zero(alu_1_carryout[1]), .isFF(alu_1_carryout[2]),
    .A_Greater(alu_1_carryout[3]), .A_Equal(alu_1_carryout[4]), .A_Smaller(alu_1_carryout[5]),
    .isODD(alu_1_carryout[6]), .isNEGATIVE(alu_1_carryout[7]));
  Decoder #(.select(2), .enable("false")) decoder_1 (
    .out0(decoder_1_out0), .out1(decoder_1_out1), .out2(decoder_1_out2), .out3(decoder_1_out3),
    .sel(regpair_1__16bit_out[15:14]));
  and and_1 (and_1_out, control_unit_1_lids_8bit_2[23], not_3_out);
  not not_3 (not_3_out, control_unit_1_pass_acc);
  // Probe on alu_1_carryout
  MemoryAccess memoryaccess_1 (
    .VerticalDecode(decoder_2_out0), .HorizontalDecode(decoder_1_out0),
    .AddressIn(regpair_1__16bit_out[11:0]), .Select(memoryaccess_1_select),
    .AddressOut(memoryaccess_1_addressout));
  MemoryAccess memoryaccess_2 (
    .VerticalDecode(decoder_2_out0), .HorizontalDecode(decoder_1_out1),
    .AddressIn(regpair_1__16bit_out[11:0]), .Select(memoryaccess_2_select),
    .AddressOut(memoryaccess_2_addressout));
  MemoryAccess memoryaccess_3 (
    .VerticalDecode(decoder_2_out0), .HorizontalDecode(decoder_1_out2),
    .AddressIn(regpair_1__16bit_out[11:0]), .Select(memoryaccess_3_select),
    .AddressOut(memoryaccess_3_addressout));
  MemoryAccess memoryaccess_4 (
    .VerticalDecode(decoder_2_out0), .HorizontalDecode(decoder_1_out3),
    .AddressIn(regpair_1__16bit_out[11:0]), .Select(memoryaccess_4_select),
    .AddressOut(memoryaccess_4_addressout));
  // Probe on regpair_1_data_high
  // Probe on regpair_1_data_low
  RegPair regpair_1 (
    .LIDS_High(control_unit_1_lids_8bit_2[23:20]), ._16bit_In(regpair_1__16bit_out),
    .LIDS_Low(control_unit_1_lids_8bit_2[19:16]), ._16bit_Out(regpair_1__16bit_out),
    .BusDataIN_High(accumulator_1_a_datain), .BusDataOUT_High(regpair_1_busdataout_high),
    .Data_High(regpair_1_data_high), .BusDataIN_Low(alu_1_carryout),
    .BusDataOUT_Low(regpair_1_busdataout_high), .Data_Low(regpair_1_data_low),
    .LIDS_Pair(control_unit_1_lids_16bit[19:16]), .CLK_H(control_unit_1_clk_pulses[10]),
    .CLK_Pair(control_unit_1_clk_pulses[4]), .CLR_H(Master_Clear_out), .CLR_Pair(Master_Clear_out),
    .CLK_L(control_unit_1_clk_pulses[9]), .CLR_L(Master_Clear_out));
  // Probe on SP_current_value
  RAM #(.addrWidth(12)) ram_1 (
    .addr(memoryaccess_1_addressout), .data(ram_1_data), .sel(memoryaccess_1_select),
    .clk(control_unit_1_enstsw_m[1]), .ld(control_unit_1_enstsw_m[0]));  // open: clr
  RAM #(.addrWidth(12)) ram_2 (
    .addr(memoryaccess_2_addressout), .data(ram_1_data), .sel(memoryaccess_2_select),
    .clk(control_unit_1_enstsw_m[1]), .ld(control_unit_1_enstsw_m[0]));  // open: clr
  RAM #(.addrWidth(12)) ram_3 (
    .addr(memoryaccess_3_addressout), .data(ram_1_data), .sel(memoryaccess_3_select),
    .clk(control_unit_1_enstsw_m[1]), .ld(control_unit_1_enstsw_m[0]));  // open: clr
  RAM #(.addrWidth(12)) ram_4 (
    .addr(memoryaccess_4_addressout), .data(ram_1_data), .sel(memoryaccess_4_select),
    .clk(control_unit_1_enstsw_m[1]), .ld(control_unit_1_enstsw_m[0]));  // open: clr
  _16bit_Register SP (
    .LIDS(control_unit_1_lids_16bit[3:0]), ._16_DataIN(regpair_1__16bit_out),
    .Current_Value(SP_current_value), ._16_DataOUT(regpair_1__16bit_out), .CLK(control_unit_1_clk_pulses[0]),
    .CLR(Master_Clear_out));
  // Probe on regpair_1_busdataout_high
  MemoryAccess memoryaccess_5 (
    .VerticalDecode(decoder_2_out1), .HorizontalDecode(decoder_1_out0),
    .AddressIn(regpair_1__16bit_out[11:0]), .Select(memoryaccess_5_select),
    .AddressOut(memoryaccess_5_addressout));
  MemoryAccess memoryaccess_6 (
    .VerticalDecode(decoder_2_out1), .HorizontalDecode(decoder_1_out1),
    .AddressIn(regpair_1__16bit_out[11:0]), .Select(memoryaccess_6_select),
    .AddressOut(memoryaccess_6_addressout));
  MemoryAccess memoryaccess_7 (
    .VerticalDecode(decoder_2_out1), .HorizontalDecode(decoder_1_out2),
    .AddressIn(regpair_1__16bit_out[11:0]), .Select(memoryaccess_7_select),
    .AddressOut(memoryaccess_7_addressout));
  MemoryAccess memoryaccess_8 (
    .VerticalDecode(decoder_2_out1), .HorizontalDecode(decoder_1_out3),
    .AddressIn(regpair_1__16bit_out[11:0]), .Select(memoryaccess_8_select),
    .AddressOut(memoryaccess_8_addressout));
  // Probe on regpair_2_data_low
  // Probe on regpair_2_data_high
  RegPair regpair_2 (
    .LIDS_High(control_unit_1_lids_8bit_2[15:12]), ._16bit_In(regpair_1__16bit_out),
    .LIDS_Low(control_unit_1_lids_8bit_2[11:8]), ._16bit_Out(regpair_1__16bit_out),
    .BusDataIN_High(regpair_1_busdataout_high), .BusDataOUT_High(regpair_1_busdataout_high),
    .Data_High(regpair_2_data_high), .BusDataIN_Low(regpair_1_busdataout_high),
    .BusDataOUT_Low(regpair_1_busdataout_high), .Data_Low(regpair_2_data_low),
    .LIDS_Pair(control_unit_1_lids_16bit[15:12]), .CLK_H(control_unit_1_clk_pulses[8]),
    .CLK_Pair(control_unit_1_clk_pulses[3]), .CLR_H(Master_Clear_out), .CLR_Pair(Master_Clear_out),
    .CLK_L(control_unit_1_clk_pulses[7]), .CLR_L(Master_Clear_out));
  // Probe on regpair_1__16bit_out
  Decoder #(.select(2), .enable("false")) decoder_2 (
    .out0(decoder_2_out0), .out1(decoder_2_out1), .out2(decoder_2_out2), .out3(decoder_2_out3),
    .sel(regpair_1__16bit_out[13:12]));
  // Probe on PC_current_value
  _16bit_Register PC (
    .LIDS(control_unit_1_lids_16bit_2), ._16_DataIN(regpair_1__16bit_out), .Current_Value(PC_current_value),
    ._16_DataOUT(regpair_1__16bit_out), .CLK(control_unit_1_clk_pulses[1]), .CLR(Master_Clear_out));
  RAM #(.addrWidth(12)) ram_5 (
    .addr(memoryaccess_5_addressout), .data(ram_1_data), .sel(memoryaccess_5_select),
    .clk(control_unit_1_enstsw_m[1]), .ld(control_unit_1_enstsw_m[0]));  // open: clr
  RAM #(.addrWidth(12)) ram_6 (
    .addr(memoryaccess_6_addressout), .data(ram_1_data), .sel(memoryaccess_6_select),
    .clk(control_unit_1_enstsw_m[1]), .ld(control_unit_1_enstsw_m[0]));  // open: clr
  RAM #(.addrWidth(12)) ram_7 (
    .addr(memoryaccess_7_addressout), .data(ram_1_data), .sel(memoryaccess_7_select),
    .clk(control_unit_1_enstsw_m[1]), .ld(control_unit_1_enstsw_m[0]));  // open: clr
  RAM #(.addrWidth(12)) ram_8 (
    .addr(memoryaccess_8_addressout), .data(ram_1_data), .sel(memoryaccess_8_select),
    .clk(control_unit_1_enstsw_m[1]), .ld(control_unit_1_enstsw_m[0]));  // open: clr
  // Probe on regpair_3_data_high
  // Probe on regpair_3_data_low
  RegPair regpair_3 (
    .LIDS_High(control_unit_1_lids_8bit_2[7:4]), ._16bit_In(regpair_1__16bit_out),
    .LIDS_Low(control_unit_1_lids_8bit), ._16bit_Out(regpair_1__16bit_out),
    .BusDataIN_High(regpair_1_busdataout_high), .BusDataOUT_High(regpair_1_busdataout_high),
    .Data_High(regpair_3_data_high), .BusDataIN_Low(regpair_1_busdataout_high),
    .BusDataOUT_Low(regpair_1_busdataout_high), .Data_Low(regpair_3_data_low),
    .LIDS_Pair(control_unit_1_lids_16bit[11:8]), .CLK_H(control_unit_1_clk_pulses[6]),
    .CLK_Pair(control_unit_1_clk_pulses[2]), .CLR_H(Master_Clear_out), .CLR_Pair(Master_Clear_out),
    .CLK_L(control_unit_1_clk_pulses[5]), .CLR_L(Master_Clear_out));
  MemoryAccess memoryaccess_9 (
    .VerticalDecode(decoder_2_out2), .HorizontalDecode(decoder_1_out0),
    .AddressIn(regpair_1__16bit_out[11:0]), .Select(memoryaccess_9_select),
    .AddressOut(memoryaccess_9_addressout));
  MemoryAccess memoryaccess_10 (
    .VerticalDecode(decoder_2_out2), .HorizontalDecode(decoder_1_out1),
    .AddressIn(regpair_1__16bit_out[11:0]), .Select(memoryaccess_10_select),
    .AddressOut(memoryaccess_10_addressout));
  MemoryAccess memoryaccess_11 (
    .VerticalDecode(decoder_2_out2), .HorizontalDecode(decoder_1_out2),
    .AddressIn(regpair_1__16bit_out[11:0]), .Select(memoryaccess_11_select),
    .AddressOut(memoryaccess_11_addressout));
  MemoryAccess memoryaccess_12 (
    .VerticalDecode(decoder_2_out2), .HorizontalDecode(decoder_1_out3),
    .AddressIn(regpair_1__16bit_out[11:0]), .Select(memoryaccess_12_select),
    .AddressOut(memoryaccess_12_addressout));
  RAM #(.addrWidth(12)) ram_9 (
    .addr(memoryaccess_9_addressout), .data(ram_1_data), .sel(memoryaccess_9_select),
    .clk(control_unit_1_enstsw_m[1]), .ld(control_unit_1_enstsw_m[0]));  // open: clr
  RAM #(.addrWidth(12)) ram_10 (
    .addr(memoryaccess_10_addressout), .data(ram_1_data), .sel(memoryaccess_10_select),
    .clk(control_unit_1_enstsw_m[1]), .ld(control_unit_1_enstsw_m[0]));  // open: clr
  RAM #(.addrWidth(12)) ram_11 (
    .addr(memoryaccess_11_addressout), .data(ram_1_data), .sel(memoryaccess_11_select),
    .clk(control_unit_1_enstsw_m[1]), .ld(control_unit_1_enstsw_m[0]));  // open: clr
  RAM #(.addrWidth(12)) ram_12 (
    .addr(memoryaccess_12_addressout), .data(ram_1_data), .sel(memoryaccess_12_select),
    .clk(control_unit_1_enstsw_m[1]), .ld(control_unit_1_enstsw_m[0]));  // open: clr
  Button CLR (.out(CLR_out));
  MemoryAccess memoryaccess_13 (
    .VerticalDecode(decoder_2_out3), .HorizontalDecode(decoder_1_out0),
    .AddressIn(regpair_1__16bit_out[11:0]), .Select(memoryaccess_13_select),
    .AddressOut(memoryaccess_13_addressout));
  MemoryAccess memoryaccess_14 (
    .VerticalDecode(decoder_2_out3), .HorizontalDecode(decoder_1_out1),
    .AddressIn(regpair_1__16bit_out[11:0]), .Select(memoryaccess_14_select),
    .AddressOut(memoryaccess_14_addressout));
  MemoryAccess memoryaccess_15 (
    .VerticalDecode(decoder_2_out3), .HorizontalDecode(decoder_1_out2),
    .AddressIn(regpair_1__16bit_out[11:0]), .Select(memoryaccess_15_select),
    .AddressOut(memoryaccess_15_addressout));
  MemoryAccess memoryaccess_16 (
    .VerticalDecode(decoder_2_out3), .HorizontalDecode(decoder_1_out3),
    .AddressIn(regpair_1__16bit_out[11:0]), .Select(memoryaccess_16_select),
    .AddressOut(memoryaccess_16_addressout));
  SIPO_Shift_Reg sipo_shift_reg_1 (
    ._8bit_Bus_IN(regpair_1_busdataout_high), .Enable(not_2_out), .Shift__1(control_unit_1_reg_shift__1),
    .CLR(CLR_out), ._24bit_Out(sipo_shift_reg_1__24bit_out), ._1bit_Instruction_IN(ram_17_data),
    ._3bit_Out(sipo_shift_reg_1__3bit_out));
  Control_Unit control_unit_1 (
    .Master_CLK(Master_Clock_out), ._8bit_DATA(regpair_1_busdataout_high),
    ._16bit_ADDRESS(regpair_1__16bit_out), .CLK_PULSES(control_unit_1_clk_pulses),
    .LIDS_8BIT({control_unit_1_lids_8bit_2, control_unit_1_lids_8bit}),
    .LIDS_16BIT({control_unit_1_lids_16bit[19:8], control_unit_1_lids_16bit_2, control_unit_1_lids_16bit[3:0]}),
    .EnStSw_M(control_unit_1_enstsw_m), .Pass_ACC(control_unit_1_pass_acc), .S(control_unit_1_s),
    ._24bit_BusIN_for_Instruction(sipo_shift_reg_1__24bit_out), .Power(not_1_out), .Reset_SC(Reset_SC),
    .Start_of_Instruction_Cycle(T0), .Reg_Shift__1(control_unit_1_reg_shift__1),
    ._24bit_BusIN_for_Instruction_2(sipo_shift_reg_1__3bit_out));  // open: IEN_0, IEN_1, CLK_IEN, LD_OUT, CLK_OUT, Show_IN
  // Probe on sipo_shift_reg_1__24bit_out
  assign ram_1_data = control_unit_1_enstsw_m[2] ? regpair_1_busdataout_high : 8'bz;  // Controlled_Buffer controlled_buffer_1
  RAM #(.addrWidth(12)) ram_13 (
    .addr(memoryaccess_13_addressout), .data(ram_1_data), .sel(memoryaccess_13_select),
    .clk(control_unit_1_enstsw_m[1]), .ld(control_unit_1_enstsw_m[0]));  // open: clr
  RAM #(.addrWidth(12)) ram_14 (
    .addr(memoryaccess_14_addressout), .data(ram_1_data), .sel(memoryaccess_14_select),
    .clk(control_unit_1_enstsw_m[1]), .ld(control_unit_1_enstsw_m[0]));  // open: clr
  RAM #(.addrWidth(12)) ram_15 (
    .addr(memoryaccess_15_addressout), .data(ram_1_data), .sel(memoryaccess_15_select),
    .clk(control_unit_1_enstsw_m[1]), .ld(control_unit_1_enstsw_m[0]));  // open: clr
  RAM #(.addrWidth(12)) ram_16 (
    .addr(memoryaccess_16_addressout), .data(ram_1_data), .sel(memoryaccess_16_select),
    .clk(control_unit_1_enstsw_m[1]), .ld(control_unit_1_enstsw_m[0]));  // open: clr
  assign regpair_1_busdataout_high = control_unit_1_enstsw_m[0] ? ram_1_data : 8'bz;  // Controlled_Buffer controlled_buffer_2
  // Probe on sipo_shift_reg_1__3bit_out
  RAM #(.addrWidth(16), .dataWidth(1)) ram_17 (
    .addr(regpair_1__16bit_out), .data(ram_17_data), .sel(not_2_out), .ld(not_2_out));  // open: clk, clr

  // Notes on the sheet:
  //   main ROM, insert instr and data
  //   isInstruction, 1 if byte is instr, 0 if byte is data
endmodule

module RegPair (
  input  [7:0] BusDataIN_High,
  input  [7:0] BusDataIN_Low,
  input  [3:0] LIDS_Low,
  input  [3:0] LIDS_High,
  input  [15:0] _16bit_In,
  input  [3:0] LIDS_Pair,
  input  CLK_H,
  input  CLR_H,
  input  CLK_L,
  input  CLR_L,
  input  CLK_Pair,
  input  CLR_Pair,
  output [7:0] BusDataOUT_High,
  output [7:0] Data_High,
  output [7:0] BusDataOUT_Low,
  output [7:0] Data_Low,
  output [15:0] _16bit_Out
);

  wire adder_2_cout, and_1_out, comparator_1_eq, controlled_buffer_3_out, not_1_out, or_1_out, or_2_out,
       or_3_out, or_4_out, or_5_out, or_6_out, or_7_out, or_8_out, or_9_out, or_10_out, or_11_out, or_12_out,
       or_13_out, or_14_out, subtractor_2_bout;
  wire [7:0] adder_1_out, adder_2_out, controlled_buffer_7_out, multiplexer_1_out, multiplexer_2_out,
       multiplexer_3_out, multiplexer_4_out, subtractor_1_out, subtractor_2_out;
  wire [15:0] controlled_buffer_1_out;

  or or_1 (or_1_out, LIDS_Pair[2], LIDS_Pair[1], LIDS_Pair[3]);
  or or_2 (or_2_out, LIDS_High[2], LIDS_High[1], LIDS_High[3]);
  or or_3 (or_3_out, LIDS_High[1], LIDS_Pair[1]);
  assign controlled_buffer_1_out = or_1_out ? _16bit_In : 16'bz;  // Controlled_Buffer controlled_buffer_1
  assign controlled_buffer_1_out[15:8] = LIDS_High[3] ? BusDataIN_High : 8'bz;  // Controlled_Buffer controlled_buffer_2
  or or_4 (or_4_out, or_2_out, or_1_out);
  or or_5 (or_5_out, LIDS_High[2], LIDS_Pair[2]);
  assign controlled_buffer_3_out = LIDS_Pair[2] ? adder_2_cout : 1'bz;  // Controlled_Buffer controlled_buffer_3
  Adder adder_1 (.a(Data_High), .b({8{1'b0}}), .out(adder_1_out), .cin(controlled_buffer_3_out));  // open: cout
  assign BusDataOUT_High = LIDS_High[0] ? Data_High : 8'bz;  // Controlled_Buffer controlled_buffer_4
  Multiplexer #(.width(8), .enable("false")) multiplexer_1 (
    .in0(controlled_buffer_1_out[15:8]), .in1(adder_1_out), .out(multiplexer_1_out), .sel(or_5_out));
  Subtractor subtractor_1 (.a(Data_High), .b({8{1'b0}}), .out(subtractor_1_out), .bin(or_12_out));  // open: bout
  Register register_1 (.D(multiplexer_2_out), .en(or_4_out), .Q(Data_High), .clk(or_6_out), .clr(or_7_out));
  Multiplexer #(.width(8), .enable("false")) multiplexer_2 (
    .in0(multiplexer_1_out), .in1(subtractor_1_out), .out(multiplexer_2_out), .sel(or_3_out));
  or or_6 (or_6_out, CLK_Pair, CLK_H);
  or or_7 (or_7_out, CLR_H, CLR_Pair);
  or or_8 (or_8_out, LIDS_Low[2], LIDS_Low[1], LIDS_Low[3]);
  or or_9 (or_9_out, LIDS_Low[1], LIDS_Pair[1]);
  assign controlled_buffer_1_out[7:0] = LIDS_Low[3] ? BusDataIN_Low : 8'bz;  // Controlled_Buffer controlled_buffer_5
  or or_10 (or_10_out, or_8_out, or_1_out);
  or or_11 (or_11_out, LIDS_Low[2], LIDS_Pair[2]);
  Adder adder_2 (.a(Data_Low), .b(8'h1), .out(adder_2_out), .cout(adder_2_cout));  // open: cin
  assign BusDataOUT_Low = LIDS_Low[0] ? Data_Low : 8'bz;  // Controlled_Buffer controlled_buffer_6
  Multiplexer #(.width(8), .enable("false")) multiplexer_3 (
    .in0(controlled_buffer_1_out[7:0]), .in1(adder_2_out), .out(multiplexer_3_out), .sel(or_11_out));
  assign controlled_buffer_7_out = not_1_out ? subtractor_2_out : 8'bz;  // Controlled_Buffer controlled_buffer_7
  Subtractor subtractor_2 (.a(Data_Low), .b(8'h1), .out(subtractor_2_out), .bout(subtractor_2_bout));  // open: bin
  or or_12 (or_12_out, subtractor_2_bout, and_1_out);
  Register register_2 (.D(multiplexer_4_out), .en(or_10_out), .Q(Data_Low), .clk(or_13_out), .clr(or_14_out));
  Multiplexer #(.width(8), .enable("false")) multiplexer_4 (
    .in0(multiplexer_3_out), .in1(controlled_buffer_7_out), .out(multiplexer_4_out), .sel(or_9_out));
  or or_13 (or_13_out, CLK_Pair, CLK_L);
  or or_14 (or_14_out, CLR_L, CLR_Pair);
  assign controlled_buffer_7_out = and_1_out ? {8{1'b1}} : 8'bz;  // Controlled_Buffer controlled_buffer_8
  and and_1 (and_1_out, or_9_out, comparator_1_eq);
  not not_1 (not_1_out, and_1_out);
  Comparator comparator_1 (.a({8{1'b0}}), .b(Data_Low), .eq(comparator_1_eq));  // open: gt, lt
  assign _16bit_Out = LIDS_Pair[0] ? {Data_Low, Data_High} : 16'bz;  // Controlled_Buffer controlled_buffer_9
endmodule

module ALU (
  input  [7:0] A,
  input  [7:0] B,
  input  [2:0] S,
  output [7:0] Output,
  output CarryOUT,
  output Zero,
  output isFF,
  output A_Greater,
  output A_Equal,
  output A_Smaller,
  output isODD,
  output isNEGATIVE
);

  wire adder_1_cout, adder_2_cout, not_1_out, subtractor_1_bout, subtractor_2_bout;
  wire [7:0] adder_1_out, adder_2_out, and_1_out, or_1_out, subtractor_1_out, subtractor_2_out, xor_1_out;

  not not_1 (not_1_out, 1'b0);
  Comparator comparator_1 (.a(A), .b(B), .gt(A_Greater), .eq(A_Equal), .lt(A_Smaller));
  Adder adder_1 (.a(A), .b(B), .out(adder_1_out), .cin(1'b0), .cout(adder_1_cout));
  Adder adder_2 (.a(A), .b(B), .out(adder_2_out), .cin(not_1_out), .cout(adder_2_cout));
  Subtractor subtractor_1 (.a(A), .b(B), .out(subtractor_1_out), .bin(1'b0), .bout(subtractor_1_bout));
  Subtractor subtractor_2 (.a(A), .b(B), .out(subtractor_2_out), .bin(not_1_out), .bout(subtractor_2_bout));
  assign and_1_out = A & B;  // AND_Gate and_1, 8 bits wide
  assign xor_1_out = A ^ B;  // XOR_Gate xor_1, 8 bits wide
  assign or_1_out = A | B;  // OR_Gate or_1, 8 bits wide
  Multiplexer #(.select(3), .width(8), .enable("false")) multiplexer_1 (
    .in0(A), .in1(adder_1_out), .in2(adder_2_out), .in3(subtractor_1_out), .in4(subtractor_2_out),
    .in5(and_1_out), .in6(xor_1_out), .in7(or_1_out), .out({isNEGATIVE, Output[6:1], isODD}), .sel(S));
  Comparator comparator_2 (.a({8{1'b1}}), .b({isNEGATIVE, Output[6:1], isODD}), .eq(isFF));  // open: gt, lt
  Comparator comparator_3 (.a({8{1'b0}}), .b({isNEGATIVE, Output[6:1], isODD}), .eq(Zero));  // open: gt, lt
  Multiplexer #(.select(3), .enable("false")) multiplexer_2 (
    .in0(1'b0), .in1(adder_1_cout), .in2(adder_2_cout), .in3(subtractor_1_bout), .in4(subtractor_2_bout),
    .in5(1'b0), .in6(1'b0), .in7(1'b0), .out(CarryOUT), .sel(S));

  assign {Output[7], Output[0]} = {isNEGATIVE, isODD};
endmodule

module Accumulator (
  input  [7:0] Bus_Input,
  input  Bus_to_ACC,
  input  [7:0] A_DataOUT,
  input  [7:0] ALU_Output,
  input  ALU_to_ACC,
  output [7:0] A_DataIN,
  output [7:0] ALU_Input
);

  assign A_DataIN = Bus_to_ACC ? Bus_Input : 8'bz;  // Controlled_Buffer controlled_buffer_1
  assign A_DataIN = ALU_to_ACC ? ALU_Output : 8'bz;  // Controlled_Buffer controlled_buffer_2

  assign ALU_Input = A_DataOUT;
endmodule

module MemoryAccess (
  input  VerticalDecode,
  input  HorizontalDecode,
  input  [11:0] AddressIn,
  output [11:0] AddressOut,
  output Select
);

  assign AddressOut = Select ? AddressIn : 12'bz;  // Controlled_Buffer controlled_buffer_1
  and and_1 (Select, VerticalDecode, HorizontalDecode);
endmodule

module _16bit_Register (
  input  [15:0] _16_DataIN,
  input  [3:0] LIDS,
  input  CLK,
  input  CLR,
  output [15:0] Current_Value,
  output [15:0] _16_DataOUT
);

  wire or_1_out;
  wire [15:0] adder_1_out, controlled_buffer_1_out, multiplexer_1_out, multiplexer_2_out, subtractor_1_out;

  assign controlled_buffer_1_out = LIDS[3] ? _16_DataIN : 16'bz;  // Controlled_Buffer controlled_buffer_1
  Multiplexer #(.width(16), .enable("false")) multiplexer_1 (
    .in0(controlled_buffer_1_out), .in1(adder_1_out), .out(multiplexer_1_out), .sel(LIDS[2]));
  Adder #(.width(16)) adder_1 (.a(Current_Value), .b(16'h1), .out(adder_1_out));  // open: cin, cout
  Multiplexer #(.width(16), .enable("false")) multiplexer_2 (
    .in0(multiplexer_1_out), .in1(subtractor_1_out), .out(multiplexer_2_out), .sel(LIDS[1]));
  Subtractor #(.width(16)) subtractor_1 (.a(Current_Value), .b(16'h1), .out(subtractor_1_out));  // open: bin, bout
  Register #(.width(16)) register_1 (.D(multiplexer_2_out), .en(or_1_out), .Q(Current_Value), .clk(CLK), .clr(CLR));
  or or_1 (or_1_out, LIDS[1], LIDS[2], LIDS[3]);
  assign _16_DataOUT = LIDS[0] ? Current_Value : 16'bz;  // Controlled_Buffer controlled_buffer_2
endmodule

module Control_Unit (
  input  Power,
  input  Reset_SC,
  input  Master_CLK,
  input  [23:0] _24bit_BusIN_for_Instruction,
  input  [2:0] _24bit_BusIN_for_Instruction_2,
  output Start_of_Instruction_Cycle,
  output Reg_Shift__1,
  output [7:0] _8bit_DATA,
  output [15:0] _16bit_ADDRESS,
  output [10:0] CLK_PULSES,
  output [23:0] LIDS_8BIT,
  output [19:0] LIDS_16BIT,
  output [2:0] EnStSw_M,
  output Pass_ACC,
  output [2:0] S,
  output IEN_0,
  output IEN_1,
  output CLK_IEN,
  output LD_OUT,
  output CLK_OUT,
  output Show_IN
);

  wire _16bit_out, alu_control_decode_1_rs_8, alu_control_decode_1_rs_b, alu_control_decode_1_rs_c,
       alu_control_decode_1_rs_d, alu_control_decode_1_rs_e, alu_control_decode_1_rs_m, ALU_out,
       alu_signal_1_clk_acc, alu_signal_1_ld_acc, alu_signal_1_show_8, alu_signal_1_show_m, and_1_out,
       clock_module_1_clk_2, clock_module_1_enable_clk, clock_module_1_set_clk, controlled_buffer_1_out,
       lids_converter_1_show_8_3, lids_converter_1_show_16_3, mov_control_decode_1_dcr_a,
       mov_control_decode_1_dcr_b, mov_control_decode_1_dcr_c, mov_control_decode_1_dcr_d,
       mov_control_decode_1_dcr_e, mov_control_decode_1_inr_a, mov_control_decode_1_inr_b,
       mov_control_decode_1_inr_c, mov_control_decode_1_inr_d, mov_control_decode_1_inr_e,
       mov_control_decode_1_rd_a, mov_control_decode_1_rd_b, mov_control_decode_1_rd_c,
       mov_control_decode_1_rd_d, mov_control_decode_1_rd_e, mov_control_decode_1_rd_m,
       mov_control_decode_1_rs_8, mov_control_decode_1_rs_a, mov_control_decode_1_rs_b,
       mov_control_decode_1_rs_c, mov_control_decode_1_rs_d, mov_control_decode_1_rs_e,
       mov_control_decode_1_rs_m, MOV_out, mov_signal_1_clk_a, mov_signal_1_clk_b, mov_signal_1_clk_c,
       mov_signal_1_clk_d, mov_signal_1_clk_e, mov_signal_1_enable_m, mov_signal_1_set_m,
       mov_signal_1_show_8, mov_signal_1_show_m, n3rd_instr_fetcher_1__24bit_load,
       n3rd_instr_fetcher_1_clk_pc, n3rd_instr_fetcher_1_decode_instruction, n3rd_instr_fetcher_1_inr_pc,
       n3rd_instr_fetcher_1_reset_sc, n3rd_instr_fetcher_1_show_m, n3rd_instr_fetcher_1_sw_pc,
       n16bit_control_decode_1_bc, n16bit_control_decode_1_dad, n16bit_control_decode_1_dcx,
       n16bit_control_decode_1_de, n16bit_control_decode_1_inx, n16bit_control_decode_1_ldax,
       n16bit_control_decode_1_ldax_16, n16bit_control_decode_1_lxi, n16bit_control_decode_1_pc,
       n16bit_control_decode_1_pop, n16bit_control_decode_1_psw, n16bit_control_decode_1_push,
       n16bit_control_decode_1_sp, n16bit_control_decode_1_stax, n16bit_control_decode_1_stax_16,
       n16bit_signal_1_clk_a, n16bit_signal_1_clk_bc, n16bit_signal_1_clk_de, n16bit_signal_1_clk_pc,
       n16bit_signal_1_clk_psw, n16bit_signal_1_clk_sp, n16bit_signal_1_enable_m, n16bit_signal_1_set_m,
       n16bit_signal_1_show_16, n16bit_signal_1_show_m, new_stepper_1_step_2, new_stepper_1_step_3,
       new_stepper_1_step_4, new_stepper_1_step_5, new_stepper_1_step_6, new_stepper_1_step_7,
       new_stepper_1_step_8, new_stepper_1_step_9, new_stepper_1_step_10, not_1_out, not_2_out, not_3_out,
       not_4_out, not_5_out, or_1_out, others_control_decode_1_call, others_control_decode_1_di,
       others_control_decode_1_ei, others_control_decode_1_in, others_control_decode_1_jmp,
       others_control_decode_1_out, others_control_decode_1_ret, Others_out, others_signal_1_clk_a,
       others_signal_1_clk_d, others_signal_1_clk_de, others_signal_1_clk_e, others_signal_1_clk_out,
       others_signal_1_clk_pc, others_signal_1_clk_sp, others_signal_1_enable_m, others_signal_1_ien_0,
       others_signal_1_ien_1, others_signal_1_ien_clk, others_signal_1_ld_out, others_signal_1_set_m,
       others_signal_1_show_16, others_signal_1_show_in, Power_q, push_pop_1_clk_high, push_pop_1_clk_low,
       push_pop_1_clk_sp, push_pop_1_enable_m, push_pop_1_set_m, push_pop_1_show_m, Reset_out;
  wire [2:0] _1st_3_out, _2nd_3_out, alu_control_decode_1_s, alu_signal_1_s_2, register_3_q;
  wire [3:0] alu_signal_1_lids_b, alu_signal_1_lids_c, alu_signal_1_lids_d, alu_signal_1_lids_de,
       alu_signal_1_lids_e, mov_signal_1_lids_a, mov_signal_1_lids_b, mov_signal_1_lids_c,
       mov_signal_1_lids_d, mov_signal_1_lids_de, mov_signal_1_lids_e, n16bit_signal_1_lids_a,
       n16bit_signal_1_lids_bc, n16bit_signal_1_lids_de, n16bit_signal_1_lids_pc, n16bit_signal_1_lids_psw,
       n16bit_signal_1_lids_sp, others_signal_1_lids_a, others_signal_1_lids_d, others_signal_1_lids_de,
       others_signal_1_lids_e, others_signal_1_lids_pc, others_signal_1_lids_sp, push_pop_1_lids_a,
       push_pop_1_lids_b, push_pop_1_lids_c, push_pop_1_lids_d, push_pop_1_lids_e, push_pop_1_lids_flags,
       push_pop_1_lids_sp;
  wire [7:0] register_1_q, register_2_q, register_2_q_3;
  wire [15:8] register_2_q_2;

  T_Flip_Flop u_Power (.Q(Power_q), .preset(Power), .reset(and_1_out));  // open: clk, T, Qn, en
  not not_1 (not_1_out, 1'b0);
  Button Reset (.out(Reset_out));
  not not_2 (not_2_out, register_1_q[7]);
  not not_3 (not_3_out, register_1_q[6]);
  not not_4 (not_4_out, register_1_q[7]);
  not not_5 (not_5_out, register_1_q[6]);
  Clock_Module clock_module_1 (
    .CLK_2(clock_module_1_clk_2), .Enable_CLK(clock_module_1_enable_clk), .Set_CLK(clock_module_1_set_clk),
    .CLK(Master_CLK), .Reset(Reset_out));  // open: D_CLK
  and MOV (MOV_out, register_1_q[7], register_1_q[6]);
  and _16bit (_16bit_out, not_2_out, register_1_q[6]);
  and ALU (ALU_out, register_1_q[7], not_3_out);
  and Others (Others_out, not_4_out, not_5_out);
  assign _1st_3_out = register_1_q[5:3];  // Buffer _1st_3, 3 bits wide
  assign _2nd_3_out = register_1_q[2:0];  // Buffer _2nd_3, 3 bits wide
  assign controlled_buffer_1_out = Power_q ? clock_module_1_clk_2 : 1'bz;  // Controlled_Buffer controlled_buffer_1
  _16bit_Control_Decode u_16bit_control_decode_1 (
    ._1st_3(_1st_3_out), ._2nd_3(_2nd_3_out), .PSW(n16bit_control_decode_1_psw),
    .BC(n16bit_control_decode_1_bc), .DE(n16bit_control_decode_1_de), .SP(n16bit_control_decode_1_sp),
    .PC(n16bit_control_decode_1_pc), .LXI(n16bit_control_decode_1_lxi), .LDAX(n16bit_control_decode_1_ldax),
    .STAX(n16bit_control_decode_1_stax), .INX(n16bit_control_decode_1_inx),
    .DCX(n16bit_control_decode_1_dcx), .DAD(n16bit_control_decode_1_dad), .POP(n16bit_control_decode_1_pop),
    .PUSH(n16bit_control_decode_1_push), .LDAX_16(n16bit_control_decode_1_ldax_16),
    .STAX_16(n16bit_control_decode_1_stax_16), .Counter_isZero(register_3_q[2]), ._16bit(_16bit_out));
  MOV_Control_Decode mov_control_decode_1 (
    .MOV(MOV_out), ._1st_3(_1st_3_out), ._2nd_3(_2nd_3_out), .DCR_A(mov_control_decode_1_dcr_a),
    .DCR_B(mov_control_decode_1_dcr_b), .DCR_C(mov_control_decode_1_dcr_c),
    .DCR_D(mov_control_decode_1_dcr_d), .DCR_E(mov_control_decode_1_dcr_e),
    .INR_A(mov_control_decode_1_inr_a), .INR_B(mov_control_decode_1_inr_b),
    .INR_C(mov_control_decode_1_inr_c), .INR_D(mov_control_decode_1_inr_d),
    .INR_E(mov_control_decode_1_inr_e), .Rd_M(mov_control_decode_1_rd_m), .Rd_E(mov_control_decode_1_rd_e),
    .Rd_D(mov_control_decode_1_rd_d), .Rd_C(mov_control_decode_1_rd_c), .Rd_B(mov_control_decode_1_rd_b),
    .Rd_A(mov_control_decode_1_rd_a), .Rs_M(mov_control_decode_1_rs_m), .Rs_E(mov_control_decode_1_rs_e),
    .Rs_D(mov_control_decode_1_rs_d), .Rs_C(mov_control_decode_1_rs_c), .Rs_B(mov_control_decode_1_rs_b),
    .Rs_8(mov_control_decode_1_rs_8), .Rs_A(mov_control_decode_1_rs_a), .Counter_isZero(register_3_q[2]));
  ALU_Control_Decode alu_control_decode_1 (
    ._1st_3(_1st_3_out), ._2nd_3(_2nd_3_out), .S(alu_control_decode_1_s), .Rs_B(alu_control_decode_1_rs_b),
    .Rs_C(alu_control_decode_1_rs_c), .Rs_D(alu_control_decode_1_rs_d), .Rs_E(alu_control_decode_1_rs_e),
    .Rs_M(alu_control_decode_1_rs_m), .Rs_8(alu_control_decode_1_rs_8), .Counter_isZero(register_3_q[2]),
    .ALU(ALU_out));
  Others_Control_Decode others_control_decode_1 (
    ._1st_3(_1st_3_out), ._2nd_3(_2nd_3_out), .JMP(others_control_decode_1_jmp),
    .CALL(others_control_decode_1_call), .RET(others_control_decode_1_ret), .DI(others_control_decode_1_di),
    .EI(others_control_decode_1_ei), .OUT(others_control_decode_1_out), .IN(others_control_decode_1_in),
    .Counter_isZero(register_3_q[2]), .Others(Others_out));
  MOV_Signal mov_signal_1 (
    .Rd_A(mov_control_decode_1_rd_a), .Rd_B(mov_control_decode_1_rd_b), .Rd_C(mov_control_decode_1_rd_c),
    .Rd_D(mov_control_decode_1_rd_d), .Rd_E(mov_control_decode_1_rd_e), .Rd_M(mov_control_decode_1_rd_m),
    .DCR_A(mov_control_decode_1_dcr_a), .DCR_B(mov_control_decode_1_dcr_b),
    .DCR_C(mov_control_decode_1_dcr_c), .DCR_D(mov_control_decode_1_dcr_d),
    .DCR_E(mov_control_decode_1_dcr_e), .INR_A(mov_control_decode_1_inr_a),
    .INR_B(mov_control_decode_1_inr_b), .INR_C(mov_control_decode_1_inr_c),
    .INR_D(mov_control_decode_1_inr_d), .INR_E(mov_control_decode_1_inr_e), .Rs_A(mov_control_decode_1_rs_a),
    .Rs_8(mov_control_decode_1_rs_8), .Rs_B(mov_control_decode_1_rs_b), .Rs_C(mov_control_decode_1_rs_c),
    .Rs_D(mov_control_decode_1_rs_d), .Rs_E(mov_control_decode_1_rs_e), .Rs_M(mov_control_decode_1_rs_m),
    .CLK_A(mov_signal_1_clk_a), .CLK_B(mov_signal_1_clk_b), .CLK_C(mov_signal_1_clk_c),
    .CLK_D(mov_signal_1_clk_d), .CLK_E(mov_signal_1_clk_e), .Enable_M(mov_signal_1_enable_m),
    .Set_M(mov_signal_1_set_m), .Show_8(mov_signal_1_show_8), .Show_M(mov_signal_1_show_m),
    .Enable_CLK(clock_module_1_enable_clk), .Set_CLK(clock_module_1_set_clk), .T0(new_stepper_1_step_5),
    .LIDS_E(mov_signal_1_lids_e), .LIDS_D(mov_signal_1_lids_d), .LIDS_B(mov_signal_1_lids_b),
    .LIDS_C(mov_signal_1_lids_c), .LIDS_A(mov_signal_1_lids_a), .LIDS_DE(mov_signal_1_lids_de));
  // Probe on register_3_q[2]
  _3rd_Instr_Fetcher u_3rd_instr_fetcher_1 (
    .SW_PC(n3rd_instr_fetcher_1_sw_pc), .Show_M(n3rd_instr_fetcher_1_show_m),
    ._24bit_Load(n3rd_instr_fetcher_1__24bit_load), .INR_PC(n3rd_instr_fetcher_1_inr_pc),
    .CLK_PC(n3rd_instr_fetcher_1_clk_pc), .Enable_CLK(clock_module_1_enable_clk),
    .Set_CLK(clock_module_1_set_clk), .T0(Start_of_Instruction_Cycle), .T1(new_stepper_1_step_2),
    .T2(new_stepper_1_step_3), .T3(new_stepper_1_step_4), .T9(new_stepper_1_step_10),
    .isINSTRUCTION(register_3_q[2]), .Decode_Instruction(n3rd_instr_fetcher_1_decode_instruction),
    .Reset_SC(n3rd_instr_fetcher_1_reset_sc), .Reg_Shift__1(Reg_Shift__1));
  or or_1 (or_1_out, Reset_SC, n3rd_instr_fetcher_1_reset_sc);
  New_Stepper new_stepper_1 (
    .Enable(not_1_out), .CLK(controlled_buffer_1_out), .Reset(or_1_out), .Step_1(Start_of_Instruction_Cycle),
    .Step_2(new_stepper_1_step_2), .Step_3(new_stepper_1_step_3), .Step_4(new_stepper_1_step_4),
    .Step_5(new_stepper_1_step_5), .Step_6(new_stepper_1_step_6), .Step_7(new_stepper_1_step_7),
    .Step_8(new_stepper_1_step_8), .Step_9(new_stepper_1_step_9), .Step_10(new_stepper_1_step_10));
  Push_Pop push_pop_1 (
    .Push(n16bit_control_decode_1_push), .PSW(n16bit_control_decode_1_psw), .BC(n16bit_control_decode_1_bc),
    .DE(n16bit_control_decode_1_de), .Pop(n16bit_control_decode_1_pop), .CLK_Low(push_pop_1_clk_low),
    .LIDS_A(push_pop_1_lids_a), .LIDS_Flags(push_pop_1_lids_flags), .LIDS_B(push_pop_1_lids_b),
    .CLK_High(push_pop_1_clk_high), .LIDS_C(push_pop_1_lids_c), .LIDS_D(push_pop_1_lids_d),
    .LIDS_E(push_pop_1_lids_e), .CLK_SP(push_pop_1_clk_sp), .Enable_M(push_pop_1_enable_m),
    .Set_M(push_pop_1_set_m), .Enable_CLK(clock_module_1_enable_clk), .Set_CLK(clock_module_1_set_clk),
    .T0(new_stepper_1_step_5), .T1(new_stepper_1_step_6), .T2(new_stepper_1_step_7),
    .T3(new_stepper_1_step_8), .Show_M(push_pop_1_show_m), .LIDS_SP(push_pop_1_lids_sp));
  _16bit_Signal u_16bit_signal_1 (
    .PSW(n16bit_control_decode_1_psw), .BC(n16bit_control_decode_1_bc), .DE(n16bit_control_decode_1_de),
    .SP(n16bit_control_decode_1_sp), .PC(n16bit_control_decode_1_pc), .LXI(n16bit_control_decode_1_lxi),
    .LDAX(n16bit_control_decode_1_ldax), .STAX(n16bit_control_decode_1_stax),
    .INX(n16bit_control_decode_1_inx), .DCX(n16bit_control_decode_1_dcx), .DAD(n16bit_control_decode_1_dad),
    .LDAX_16(n16bit_control_decode_1_ldax_16), .STAX_16(n16bit_control_decode_1_stax_16),
    .CLK_PSW(n16bit_signal_1_clk_psw), .CLK_BC(n16bit_signal_1_clk_bc), .CLK_DE(n16bit_signal_1_clk_de),
    .CLK_SP(n16bit_signal_1_clk_sp), .CLK_PC(n16bit_signal_1_clk_pc), .Show_16(n16bit_signal_1_show_16),
    .Show_M(n16bit_signal_1_show_m), .Enable_M(n16bit_signal_1_enable_m), .Set_M(n16bit_signal_1_set_m),
    .CLK_A(n16bit_signal_1_clk_a), .Enable_CLK(clock_module_1_enable_clk), .Set_CLK(clock_module_1_set_clk),
    .T0(new_stepper_1_step_5), .LIDS_PSW(n16bit_signal_1_lids_psw), .LIDS_BC(n16bit_signal_1_lids_bc),
    .LIDS_DE(n16bit_signal_1_lids_de), .LIDS_SP(n16bit_signal_1_lids_sp), .LIDS_PC(n16bit_signal_1_lids_pc),
    .LIDS_A(n16bit_signal_1_lids_a));
  ALU_Signal alu_signal_1 (
    .S(alu_control_decode_1_s), .Rs_B(alu_control_decode_1_rs_b), .Rs_C(alu_control_decode_1_rs_c),
    .Rs_D(alu_control_decode_1_rs_d), .Rs_E(alu_control_decode_1_rs_e), .Rs_M(alu_control_decode_1_rs_m),
    .Rs_8(alu_control_decode_1_rs_8), .S_2(alu_signal_1_s_2), .Show_M(alu_signal_1_show_m),
    .Show_8(alu_signal_1_show_8), .LD_ACC(alu_signal_1_ld_acc), .CLK_ACC(alu_signal_1_clk_acc),
    .Enable_CLK(clock_module_1_enable_clk), .Set_CLK(clock_module_1_set_clk), .T0(new_stepper_1_step_5),
    .LIDS_B(alu_signal_1_lids_b), .LIDS_C(alu_signal_1_lids_c), .LIDS_D(alu_signal_1_lids_d),
    .LIDS_E(alu_signal_1_lids_e), .LIDS_DE(alu_signal_1_lids_de));
  Others_Signal others_signal_1 (
    .JMP(others_control_decode_1_jmp), .CALL(others_control_decode_1_call),
    .RET(others_control_decode_1_ret), .DI(others_control_decode_1_di), .EI(others_control_decode_1_ei),
    .OUT(others_control_decode_1_out), .IN(others_control_decode_1_in), .CLK_PC(others_signal_1_clk_pc),
    .CLK_DE(others_signal_1_clk_de), .CLK_SP(others_signal_1_clk_sp), .Enable_M(others_signal_1_enable_m),
    .Set_M(others_signal_1_set_m), .CLK_E(others_signal_1_clk_e), .CLK_D(others_signal_1_clk_d),
    .IEN_0(others_signal_1_ien_0), .IEN_1(others_signal_1_ien_1), .IEN_CLK(others_signal_1_ien_clk),
    .LD_OUT(others_signal_1_ld_out), .CLK_OUT(others_signal_1_clk_out), .Show_IN(others_signal_1_show_in),
    .CLK_A(others_signal_1_clk_a), .Enable_CLK(clock_module_1_enable_clk), .Set_CLK(clock_module_1_set_clk),
    .T0(new_stepper_1_step_5), .T1(new_stepper_1_step_6), .T2(new_stepper_1_step_7),
    .T3(new_stepper_1_step_8), .T4(new_stepper_1_step_9), .Show_16(others_signal_1_show_16),
    .LIDS_A(others_signal_1_lids_a), .LIDS_D(others_signal_1_lids_d), .LIDS_E(others_signal_1_lids_e),
    .LIDS_DE(others_signal_1_lids_de), .LIDS_PC(others_signal_1_lids_pc), .LIDS_SP(others_signal_1_lids_sp));
  LIDS_converter lids_converter_1 (
    .CLK_A(mov_signal_1_clk_a), .CLK_B(mov_signal_1_clk_b), .CLK_C(mov_signal_1_clk_c),
    .CLK_D(mov_signal_1_clk_d), .CLK_E(mov_signal_1_clk_e), .Enable_M(mov_signal_1_enable_m),
    .Set_M(mov_signal_1_set_m), .Show_8(mov_signal_1_show_8), .Show_M_2(mov_signal_1_show_m),
    .LIDS_DE(mov_signal_1_lids_de), .LIDS_A(mov_signal_1_lids_a), .LIDS_B(mov_signal_1_lids_b),
    .LIDS_C(mov_signal_1_lids_c), .LIDS_D(mov_signal_1_lids_d), .LIDS_E(mov_signal_1_lids_e),
    .CLK_Low(push_pop_1_clk_low), .CLK_High(push_pop_1_clk_high), .CLK_SP(push_pop_1_clk_sp),
    .LIDS_A_2(push_pop_1_lids_a), .LIDS_Flags(push_pop_1_lids_flags), .LIDS_B_2(push_pop_1_lids_b),
    .LIDS_C_2(push_pop_1_lids_c), .LIDS_D_2(push_pop_1_lids_d), .LIDS_E_2(push_pop_1_lids_e),
    .LIDS_SP(push_pop_1_lids_sp), .Enable_M_2(push_pop_1_enable_m), .Set_M_2(push_pop_1_set_m),
    .Show_M_3(push_pop_1_show_m), .CLK_PSW(n16bit_signal_1_clk_psw), .CLK_BC(n16bit_signal_1_clk_bc),
    .CLK_DE(n16bit_signal_1_clk_de), .CLK_SP_2(n16bit_signal_1_clk_sp), .CLK_PC_2(n16bit_signal_1_clk_pc),
    .CLK_A_2(n16bit_signal_1_clk_a), .LIDS_PSW(n16bit_signal_1_lids_psw), .LIDS_BC(n16bit_signal_1_lids_bc),
    .LIDS_DE_2(n16bit_signal_1_lids_de), .LIDS_SP_2(n16bit_signal_1_lids_sp),
    .LIDS_PC(n16bit_signal_1_lids_pc), .LIDS_A_3(n16bit_signal_1_lids_a), .Show_16(n16bit_signal_1_show_16),
    .Show_M_4(n16bit_signal_1_show_m), .Enable_M_3(n16bit_signal_1_enable_m),
    .Set_M_3(n16bit_signal_1_set_m), .S(alu_signal_1_s_2), .LIDS_B_3(alu_signal_1_lids_b),
    .LIDS_C_3(alu_signal_1_lids_c), .LIDS_D_3(alu_signal_1_lids_d), .LIDS_E_3(alu_signal_1_lids_e),
    .LIDS_DE_3(alu_signal_1_lids_de), .Show_M_5(alu_signal_1_show_m), .Show_8_2(alu_signal_1_show_8),
    .LD_ACC(alu_signal_1_ld_acc), .CLK_ACC(alu_signal_1_clk_acc), .CLK_A_3(others_signal_1_clk_a),
    .CLK_D_2(others_signal_1_clk_d), .CLK_E_2(others_signal_1_clk_e), .CLK_DE_2(others_signal_1_clk_de),
    .CLK_PC_3(others_signal_1_clk_pc), .CLK_SP_3(others_signal_1_clk_sp),
    .Enable_M_4(others_signal_1_enable_m), .Set_M_4(others_signal_1_set_m), .IEN_0(others_signal_1_ien_0),
    .IEN_1(others_signal_1_ien_1), .CLK_IEN(others_signal_1_ien_clk), .LD_OUT(others_signal_1_ld_out),
    .CLK_OUT(others_signal_1_clk_out), .Show_IN(others_signal_1_show_in),
    .Show_16_2(others_signal_1_show_16), .LIDS_A_4(others_signal_1_lids_a),
    .LIDS_D_4(others_signal_1_lids_d), .LIDS_E_4(others_signal_1_lids_e),
    .LIDS_DE_4(others_signal_1_lids_de), .LIDS_PC_2(others_signal_1_lids_pc),
    .LIDS_SP_3(others_signal_1_lids_sp), .Show_16_3(lids_converter_1_show_16_3),
    .Show_8_3(lids_converter_1_show_8_3), .IEN_0_2(IEN_0), .IEN_1_2(IEN_1), .CLK_IEN_2(CLK_IEN),
    .LD_OUT_2(LD_OUT), .CLK_OUT_2(CLK_OUT), .Show_IN_2(Show_IN), .S_2(S), .Pass_ACC(Pass_ACC),
    .SW_PC(n3rd_instr_fetcher_1_sw_pc), .Show_M(n3rd_instr_fetcher_1_show_m),
    .INR_PC(n3rd_instr_fetcher_1_inr_pc), .CLK_PC(n3rd_instr_fetcher_1_clk_pc), .CLK_PULSES(CLK_PULSES),
    .LIDS_8BIT(LIDS_8BIT), .LIDS_16BIT(LIDS_16BIT), .EnStSw_M(EnStSw_M));
  Register register_1 (
    .D(register_2_q_3), .en(not_1_out), .Q(register_1_q), .clk(n3rd_instr_fetcher_1_decode_instruction));  // open: clr
  // Probe on register_1_q
  Register #(.width(24)) register_2 (
    .D(_24bit_BusIN_for_Instruction), .en(not_1_out), .Q({register_2_q_3, register_2_q_2, register_2_q}),
    .clk(n3rd_instr_fetcher_1__24bit_load));  // open: clr
  // Probe on {register_2_q_3, register_2_q_2, register_2_q}
  Register #(.width(3)) register_3 (
    .D(_24bit_BusIN_for_Instruction_2), .en(not_1_out), .Q(register_3_q),
    .clk(n3rd_instr_fetcher_1__24bit_load));  // open: clr
  // Probe on register_3_q
  and and_1 (and_1_out, register_1_q[0], register_1_q[1], register_1_q[2], register_1_q[3], register_1_q[4], register_1_q[5], register_1_q[6], register_1_q[7]);
  assign _8bit_DATA = lids_converter_1_show_8_3 ? register_2_q_2 : 8'bz;  // Controlled_Buffer controlled_buffer_2
  assign _16bit_ADDRESS = lids_converter_1_show_16_3 ? {register_2_q_2, register_2_q} : 16'bz;  // Controlled_Buffer controlled_buffer_3
  // NAND_Gate nand_1 is placed but not wired
endmodule

module Clock_Module (
  input  CLK,
  input  Reset,
  output CLK_2,
  output Enable_CLK,
  output Set_CLK,
  output D_CLK
);

  wire counter_1_carry, decoder_1_out0, decoder_1_out1, decoder_1_out2, decoder_1_out3, decoder_1_out4,
       decoder_1_out5, decoder_1_out6, decoder_1_out7, or_1_out, or_2_out, or_3_out;
  wire [2:0] counter_1_q;

  Counter #(.width(3), .max('h7)) counter_1 (
    .count(1'b1), .Q(counter_1_q), .carry(counter_1_carry), .clk(CLK), .clr(or_1_out));  // open: load, D
  or or_1 (or_1_out, Reset, decoder_1_out7);
  Decoder #(.select(3), .enable("false")) decoder_1 (
    .out0(decoder_1_out0), .out1(decoder_1_out1), .out2(decoder_1_out2), .out3(decoder_1_out3),
    .out4(decoder_1_out4), .out5(decoder_1_out5), .out6(decoder_1_out6), .out7(decoder_1_out7),
    .sel(counter_1_q));
  or or_2 (or_2_out, decoder_1_out0, decoder_1_out1, decoder_1_out2, decoder_1_out3);
  or or_3 (or_3_out, decoder_1_out2, decoder_1_out3, decoder_1_out4, decoder_1_out5);
  buf u_CLK (CLK_2, or_2_out);
  or u_Enable_CLK (Enable_CLK, or_2_out, or_3_out);
  and u_Set_CLK (Set_CLK, or_2_out, or_3_out);
  buf u_D_CLK (D_CLK, or_3_out);
endmodule

module MOV_Control_Decode (
  input  Counter_isZero,
  input  MOV,
  input  [2:0] _1st_3,
  input  [2:0] _2nd_3,
  output Rd_M,
  output Rd_E,
  output Rd_D,
  output Rd_C,
  output Rd_B,
  output Rd_A,
  output DCR_A,
  output DCR_B,
  output DCR_C,
  output DCR_D,
  output DCR_E,
  output INR_A,
  output INR_B,
  output INR_C,
  output INR_D,
  output INR_E,
  output Rs_M,
  output Rs_E,
  output Rs_D,
  output Rs_C,
  output Rs_B,
  output Rs_8,
  output Rs_A
);

  wire and_1_out, DCR_out, decoder_1_out0, decoder_1_out1, decoder_1_out2, decoder_1_out3, decoder_1_out4,
       decoder_1_out5, decoder_1_out6, decoder_1_out7, decoder_2_out0, decoder_2_out1, decoder_2_out2,
       decoder_2_out3, decoder_2_out4, decoder_2_out5, decoder_2_out6, decoder_2_out7, INR_out, not_1_out,
       not_2_out, not_3_out, not_4_out, Rd_A_2_out, Rd_B_2_out, Rd_C_2_out, Rd_D_2_out, Rd_E_2_out,
       Rd_M_2_out, Rs_8_out, Rs_A_out, Rs_B_out, Rs_C_out, Rs_D_out, Rs_E_out, Rs_M_out;

  and INR (INR_out, and_1_out, decoder_1_out7);
  and and_1 (and_1_out, Counter_isZero, MOV);
  Decoder #(.select(3), .enable("false")) decoder_1 (
    .out0(decoder_1_out0), .out1(decoder_1_out1), .out2(decoder_1_out2), .out3(decoder_1_out3),
    .out4(decoder_1_out4), .out5(decoder_1_out5), .out6(decoder_1_out6), .out7(decoder_1_out7), .sel(_1st_3));
  Decoder #(.select(3), .enable("false")) decoder_2 (
    .out0(decoder_2_out0), .out1(decoder_2_out1), .out2(decoder_2_out2), .out3(decoder_2_out3),
    .out4(decoder_2_out4), .out5(decoder_2_out5), .out6(decoder_2_out6), .out7(decoder_2_out7), .sel(_2nd_3));
  and DCR (DCR_out, and_1_out, decoder_2_out7);
  and u_Rd_E (Rd_E, Rd_E_2_out, not_4_out, not_1_out);
  and u_Rd_M (Rd_M, Rd_M_2_out, not_4_out, not_1_out);
  not not_1 (not_1_out, INR_out);
  and Rd_M_2 (Rd_M_2_out, and_1_out, decoder_1_out6);
  and Rd_E_2 (Rd_E_2_out, and_1_out, decoder_1_out5);
  and u_Rs_M (Rs_M_out, and_1_out, decoder_2_out6);
  and u_Rs_E (Rs_E_out, and_1_out, decoder_2_out5);
  not not_2 (not_2_out, DCR_out);
  and Rs_M_2 (Rs_M, Rs_M_out, not_3_out, not_2_out);
  and Rs_E_2 (Rs_E, Rs_E_out, not_3_out, not_2_out);
  and u_Rd_B (Rd_B, Rd_B_2_out, not_4_out, not_1_out);
  and u_Rd_D (Rd_D, Rd_D_2_out, not_4_out, not_1_out);
  and u_Rd_C (Rd_C, Rd_C_2_out, not_4_out, not_1_out);
  and Rd_C_2 (Rd_C_2_out, and_1_out, decoder_1_out3);
  and Rd_D_2 (Rd_D_2_out, and_1_out, decoder_1_out4);
  and Rd_B_2 (Rd_B_2_out, and_1_out, decoder_1_out2);
  and u_Rs_C (Rs_C_out, and_1_out, decoder_2_out3);
  and u_Rs_D (Rs_D_out, and_1_out, decoder_2_out4);
  and u_Rs_B (Rs_B_out, and_1_out, decoder_2_out2);
  and Rs_B_2 (Rs_B, Rs_B_out, not_3_out, not_2_out);
  and Rs_C_2 (Rs_C, Rs_C_out, not_3_out, not_2_out);
  and Rs_D_2 (Rs_D, Rs_D_out, not_3_out, not_2_out);
  and u_Rd_A (Rd_A, Rd_A_2_out, not_4_out, not_1_out);
  and Rd_A_2 (Rd_A_2_out, and_1_out, decoder_1_out0);
  and u_Rs_A (Rs_A_out, and_1_out, decoder_2_out0);
  and u_Rs_8 (Rs_8_out, and_1_out, decoder_2_out1);
  not not_3 (not_3_out, INR_out);
  and Rs_A_2 (Rs_A, Rs_A_out, not_3_out, not_2_out);
  and Rs_8_2 (Rs_8, Rs_8_out, not_3_out, not_2_out);
  not not_4 (not_4_out, DCR_out);
  and u_DCR_A (DCR_A, DCR_out, decoder_1_out0);
  and u_DCR_B (DCR_B, DCR_out, decoder_1_out2);
  and u_DCR_C (DCR_C, DCR_out, decoder_1_out3);
  and u_DCR_D (DCR_D, DCR_out, decoder_1_out4);
  and u_DCR_E (DCR_E, DCR_out, decoder_1_out5);
  and u_INR_A (INR_A, decoder_2_out0, INR_out);
  and u_INR_B (INR_B, decoder_2_out2, INR_out);
  and u_INR_C (INR_C, decoder_2_out3, INR_out);
  and u_INR_D (INR_D, decoder_2_out4, INR_out);
  and u_INR_E (INR_E, decoder_2_out5, INR_out);
endmodule

module ALU_Control_Decode (
  input  Counter_isZero,
  input  ALU,
  input  [2:0] _1st_3,
  input  [2:0] _2nd_3,
  output [2:0] S,
  output Rs_B,
  output Rs_C,
  output Rs_D,
  output Rs_E,
  output Rs_M,
  output Rs_8
);

  wire _8_out, and_1_out, B_out, C_out, D_out, decoder_1_out2, decoder_1_out3, decoder_1_out4,
       decoder_1_out5, decoder_1_out6, decoder_1_out7, E_out, M_out;

  and and_1 (and_1_out, Counter_isZero, ALU);
  Decoder #(.select(3), .enable("false")) decoder_1 (
    .out2(decoder_1_out2), .out3(decoder_1_out3), .out4(decoder_1_out4), .out5(decoder_1_out5),
    .out6(decoder_1_out6), .out7(decoder_1_out7), .sel(_2nd_3));  // open: out0, out1
  assign S = and_1_out ? _1st_3 : 3'bz;  // Controlled_Buffer controlled_buffer_1
  buf B (B_out, decoder_1_out2);
  buf C (C_out, decoder_1_out3);
  buf D (D_out, decoder_1_out4);
  buf E (E_out, decoder_1_out5);
  buf M (M_out, decoder_1_out6);
  buf _8 (_8_out, decoder_1_out7);
  and u_Rs_B (Rs_B, and_1_out, B_out);
  and u_Rs_C (Rs_C, and_1_out, C_out);
  and u_Rs_D (Rs_D, and_1_out, D_out);
  and u_Rs_E (Rs_E, E_out, and_1_out);
  and u_Rs_M (Rs_M, M_out, and_1_out);
  and u_Rs_8 (Rs_8, _8_out, and_1_out);
endmodule

module _16bit_Control_Decode (
  input  Counter_isZero,
  input  _16bit,
  input  [2:0] _1st_3,
  input  [2:0] _2nd_3,
  output PSW,
  output BC,
  output DE,
  output SP,
  output PC,
  output LXI,
  output LDAX,
  output STAX,
  output INX,
  output DCX,
  output DAD,
  output POP,
  output PUSH,
  output LDAX_16,
  output STAX_16
);

  wire and_1_out, and_13_out, and_14_out, BC_out, DAD_out, DCX_out, DE_out, decoder_1_out1, decoder_1_out2,
       decoder_1_out3, decoder_1_out4, decoder_1_out5, decoder_2_out0, decoder_2_out1, decoder_2_out2,
       decoder_2_out3, decoder_2_out4, decoder_2_out5, decoder_2_out6, decoder_2_out7, INX_out, LDAX_out,
       LXI_out, not_1_out, PC_out, POP_out, PSW_out, PUSH_out, SP_out, STAX_out;

  and and_1 (and_1_out, Counter_isZero, _16bit);
  Decoder #(.select(3), .enable("false")) decoder_1 (
    .out1(decoder_1_out1), .out2(decoder_1_out2), .out3(decoder_1_out3), .out4(decoder_1_out4),
    .out5(decoder_1_out5), .sel(_1st_3));  // open: out0, out6, out7
  Decoder #(.select(3), .enable("false")) decoder_2 (
    .out0(decoder_2_out0), .out1(decoder_2_out1), .out2(decoder_2_out2), .out3(decoder_2_out3),
    .out4(decoder_2_out4), .out5(decoder_2_out5), .out6(decoder_2_out6), .out7(decoder_2_out7), .sel(_2nd_3));
  buf u_PSW (PSW_out, decoder_1_out1);
  buf u_BC (BC_out, decoder_1_out2);
  buf u_DE (DE_out, decoder_1_out3);
  buf u_SP (SP_out, decoder_1_out4);
  buf u_PC (PC_out, decoder_1_out5);
  buf u_LXI (LXI_out, decoder_2_out0);
  buf u_LDAX (LDAX_out, decoder_2_out1);
  buf u_STAX (STAX_out, decoder_2_out2);
  buf u_INX (INX_out, decoder_2_out3);
  buf u_DCX (DCX_out, decoder_2_out4);
  buf u_DAD (DAD_out, decoder_2_out5);
  buf u_POP (POP_out, decoder_2_out6);
  buf u_PUSH (PUSH_out, decoder_2_out7);
  and and_2 (PSW, and_1_out, PSW_out);
  and and_3 (BC, and_1_out, BC_out);
  and and_4 (DE, and_1_out, DE_out);
  and and_5 (SP, and_1_out, SP_out);
  and and_6 (PC, and_1_out, PC_out);
  not not_1 (not_1_out, SP);
  and and_7 (LXI, and_1_out, LXI_out);
  and and_8 (LDAX, and_1_out, LDAX_out);
  and and_9 (STAX, and_1_out, STAX_out);
  and and_10 (INX, and_1_out, INX_out);
  and and_11 (DCX, and_1_out, DCX_out);
  and and_12 (DAD, and_1_out, DAD_out);
  and and_13 (and_13_out, and_1_out, POP_out);
  assign POP = not_1_out ? and_13_out : 1'bz;  // Controlled_Buffer controlled_buffer_1
  and and_14 (and_14_out, and_1_out, PUSH_out);
  and and_15 (LDAX_16, and_13_out, SP);
  and and_16 (STAX_16, and_14_out, SP);
  assign PUSH = not_1_out ? and_14_out : 1'bz;  // Controlled_Buffer controlled_buffer_2
endmodule

module Others_Control_Decode (
  input  Counter_isZero,
  input  Others,
  input  [2:0] _1st_3,
  input  [2:0] _2nd_3,
  output JMP,
  output CALL,
  output RET,
  output DI,
  output EI,
  output OUT,
  output IN
);

  wire and_1_out, and_2_out, CALL_out, decoder_1_out0, decoder_1_out1, decoder_1_out2, decoder_1_out3,
       decoder_1_out4, decoder_1_out5, decoder_1_out6, decoder_1_out7, DI_out, EI_out, IN_out, JMP_out,
       OUT_out, RET_out;
  wire [2:0] not_1_out;

  and and_1 (and_1_out, Counter_isZero, Others);
  assign not_1_out = ~_1st_3;  // NOT_Gate not_1, 3 bits wide
  Decoder #(.select(3), .enable("false")) decoder_1 (
    .out0(decoder_1_out0), .out1(decoder_1_out1), .out2(decoder_1_out2), .out3(decoder_1_out3),
    .out4(decoder_1_out4), .out5(decoder_1_out5), .out6(decoder_1_out6), .out7(decoder_1_out7), .sel(_2nd_3));
  and and_2 (and_2_out, and_1_out, not_1_out[0], not_1_out[1], not_1_out[2]);
  buf u_JMP (JMP_out, decoder_1_out1);
  buf u_CALL (CALL_out, decoder_1_out2);
  buf u_RET (RET_out, decoder_1_out3);
  buf u_DI (DI_out, decoder_1_out4);
  buf u_EI (EI_out, decoder_1_out5);
  buf u_OUT (OUT_out, decoder_1_out6);
  buf u_IN (IN_out, decoder_1_out7);
  and and_3 (JMP, and_2_out, JMP_out);
  and and_4 (CALL, and_2_out, CALL_out);
  and and_5 (RET, and_2_out, RET_out);
  and and_6 (DI, and_2_out, DI_out);
  and and_7 (EI, and_2_out, EI_out);
  and and_8 (OUT, and_2_out, OUT_out);
  and and_9 (IN, and_2_out, IN_out);
endmodule

module MOV_Signal (
  input  Enable_CLK,
  input  Set_CLK,
  input  T0,
  input  Rd_A,
  input  Rd_B,
  input  Rd_C,
  input  Rd_D,
  input  Rd_E,
  input  Rd_M,
  input  DCR_A,
  input  DCR_B,
  input  DCR_C,
  input  DCR_D,
  input  DCR_E,
  input  INR_A,
  input  INR_B,
  input  INR_C,
  input  INR_D,
  input  INR_E,
  input  Rs_A,
  input  Rs_8,
  input  Rs_B,
  input  Rs_C,
  input  Rs_D,
  input  Rs_E,
  input  Rs_M,
  output CLK_A,
  output CLK_B,
  output CLK_C,
  output CLK_D,
  output CLK_E,
  output Enable_M,
  output Set_M,
  output Show_8,
  output Show_M,
  output [3:0] LIDS_A,
  output [3:0] LIDS_B,
  output [3:0] LIDS_C,
  output [3:0] LIDS_D,
  output [3:0] LIDS_E,
  output [3:0] LIDS_DE
);

  wire and_2_out, and_4_out, and_6_out, and_8_out, and_10_out, and_14_out, and_16_out, and_18_out,
       and_20_out, and_22_out, and_24_out, and_26_out, and_28_out, and_30_out, and_32_out;

  and and_1 (LIDS_A[3], Rd_A, T0, Enable_CLK);
  and and_2 (and_2_out, Rd_A, T0, Set_CLK);
  and and_3 (LIDS_B[3], Rd_B, T0, Enable_CLK);
  and and_4 (and_4_out, Rd_B, T0, Set_CLK);
  and and_5 (LIDS_C[3], Rd_C, T0, Enable_CLK);
  and and_6 (and_6_out, Rd_C, T0, Set_CLK);
  and and_7 (LIDS_D[3], Rd_D, T0, Enable_CLK);
  and and_8 (and_8_out, Rd_D, T0, Set_CLK);
  and and_9 (LIDS_E[3], Rd_E, T0, Enable_CLK);
  and and_10 (and_10_out, Rd_E, T0, Set_CLK);
  and and_11 (Enable_M, Rd_M, T0, Enable_CLK);
  and and_12 (Set_M, Rd_M, T0, Set_CLK);
  and and_13 (LIDS_A[1], DCR_A, T0, Enable_CLK);
  and and_14 (and_14_out, DCR_A, T0, Set_CLK);
  and and_15 (LIDS_B[1], DCR_B, T0, Enable_CLK);
  and and_16 (and_16_out, DCR_B, T0, Set_CLK);
  and and_17 (LIDS_C[1], DCR_C, T0, Enable_CLK);
  and and_18 (and_18_out, DCR_C, T0, Set_CLK);
  and and_19 (LIDS_D[1], DCR_D, T0, Enable_CLK);
  and and_20 (and_20_out, DCR_D, T0, Set_CLK);
  and and_21 (LIDS_E[1], DCR_E, T0, Enable_CLK);
  and and_22 (and_22_out, DCR_E, T0, Set_CLK);
  and and_23 (LIDS_A[2], INR_A, T0, Enable_CLK);
  and and_24 (and_24_out, INR_A, T0, Set_CLK);
  and and_25 (LIDS_B[2], INR_B, T0, Enable_CLK);
  and and_26 (and_26_out, INR_B, T0, Set_CLK);
  and and_27 (LIDS_C[2], INR_C, T0, Enable_CLK);
  and and_28 (and_28_out, INR_C, T0, Set_CLK);
  and and_29 (LIDS_D[2], INR_D, T0, Enable_CLK);
  and and_30 (and_30_out, INR_D, T0, Set_CLK);
  and and_31 (LIDS_E[2], INR_E, T0, Enable_CLK);
  and and_32 (and_32_out, INR_E, T0, Set_CLK);
  and and_33 (LIDS_A[0], Rs_A, T0, Enable_CLK);
  and and_34 (Show_8, Rs_8, T0, Enable_CLK);
  and and_35 (LIDS_B[0], Rs_B, T0, Enable_CLK);
  and and_36 (LIDS_C[0], Rs_C, T0, Enable_CLK);
  and and_37 (LIDS_D[0], Rs_D, T0, Enable_CLK);
  and and_38 (LIDS_E[0], Rs_E, T0, Enable_CLK);
  and and_39 (Show_M, Rs_M, T0, Enable_CLK);
  or or_1 (CLK_A, and_2_out, and_14_out, and_24_out);
  or or_2 (CLK_B, and_4_out, and_16_out, and_26_out);
  or or_3 (CLK_C, and_6_out, and_18_out, and_28_out);
  or or_4 (CLK_D, and_8_out, and_20_out, and_30_out);
  or or_5 (CLK_E, and_10_out, and_22_out, and_32_out);
  or or_6 (LIDS_DE[0], Enable_M, Show_M);

  assign LIDS_DE[3:1] = 3'b000;
endmodule

module _16bit_Signal (
  input  Enable_CLK,
  input  Set_CLK,
  input  T0,
  input  PSW,
  input  BC,
  input  DE,
  input  SP,
  input  PC,
  input  LXI,
  input  LDAX,
  input  STAX,
  input  INX,
  input  DCX,
  input  DAD,
  input  LDAX_16,
  input  STAX_16,
  output CLK_PSW,
  output [3:0] LIDS_PSW,
  output CLK_BC,
  output [3:0] LIDS_BC,
  output CLK_DE,
  output [3:0] LIDS_DE,
  output CLK_SP,
  output [3:0] LIDS_SP,
  output CLK_PC,
  output [3:0] LIDS_PC,
  output Show_16,
  output Show_M,
  output Enable_M,
  output Set_M,
  output CLK_A,
  output [3:0] LIDS_A
);

  wire and_2_out, and_3_out, and_4_out, and_5_out, and_6_out, and_8_out, and_10_out, and_12_out, and_13_out,
       and_14_out, and_15_out, and_16_out, and_18_out, and_20_out, and_22_out, and_23_out, and_24_out,
       and_25_out, and_26_out, and_28_out, and_30_out, and_32_out, and_33_out, and_34_out, and_35_out,
       and_36_out, and_38_out, and_40_out, and_41_out, and_42_out, and_43_out, and_44_out, and_46_out,
       and_47_out, and_48_out, and_49_out, and_50_out, and_52_out, and_54_out, or_7_out, or_10_out,
       or_11_out, or_12_out, or_13_out, or_14_out, or_15_out;

  and and_1 (LIDS_PSW[3], PSW, T0, LXI, Enable_CLK);
  and and_2 (and_2_out, PSW, T0, LXI, Set_CLK);
  and and_3 (and_3_out, PSW, T0, LDAX, Enable_CLK);
  and and_4 (and_4_out, PSW, T0, LDAX, Set_CLK);
  and and_5 (and_5_out, PSW, T0, STAX, Enable_CLK);
  and and_6 (and_6_out, PSW, T0, STAX, Set_CLK);
  and and_7 (LIDS_PSW[2], PSW, T0, INX, Enable_CLK);
  and and_8 (and_8_out, PSW, T0, INX, Set_CLK);
  and and_9 (LIDS_PSW[1], PSW, T0, DCX, Enable_CLK);
  and and_10 (and_10_out, PSW, T0, DCX, Set_CLK);
  and and_11 (LIDS_BC[3], BC, T0, LXI, Enable_CLK);
  and and_12 (and_12_out, BC, T0, LXI, Set_CLK);
  and and_13 (and_13_out, BC, T0, LDAX, Enable_CLK);
  and and_14 (and_14_out, BC, T0, LDAX, Set_CLK);
  and and_15 (and_15_out, BC, T0, STAX, Enable_CLK);
  and and_16 (and_16_out, BC, T0, STAX, Set_CLK);
  and and_17 (LIDS_BC[2], BC, T0, INX, Enable_CLK);
  and and_18 (and_18_out, BC, T0, INX, Set_CLK);
  and and_19 (LIDS_BC[1], BC, T0, DCX, Enable_CLK);
  and and_20 (and_20_out, BC, T0, DCX, Set_CLK);
  and and_21 (LIDS_DE[3], DE, T0, LXI, Enable_CLK);
  and and_22 (and_22_out, DE, T0, LXI, Set_CLK);
  and and_23 (and_23_out, DE, T0, LDAX, Enable_CLK);
  and and_24 (and_24_out, DE, T0, LDAX, Set_CLK);
  and and_25 (and_25_out, DE, T0, STAX, Enable_CLK);
  and and_26 (and_26_out, DE, T0, STAX, Set_CLK);
  and and_27 (LIDS_DE[2], DE, T0, INX, Enable_CLK);
  and and_28 (and_28_out, DE, T0, INX, Set_CLK);
  and and_29 (LIDS_DE[1], DE, T0, DCX, Enable_CLK);
  and and_30 (and_30_out, DE, T0, DCX, Set_CLK);
  and and_31 (LIDS_SP[3], SP, T0, LXI, Enable_CLK);
  and and_32 (and_32_out, SP, T0, LXI, Set_CLK);
  and and_33 (and_33_out, SP, T0, LDAX, Enable_CLK);
  and and_34 (and_34_out, SP, T0, LDAX, Set_CLK);
  and and_35 (and_35_out, SP, T0, STAX, Enable_CLK);
  and and_36 (and_36_out, SP, T0, STAX, Set_CLK);
  and and_37 (LIDS_SP[2], SP, T0, INX, Enable_CLK);
  and and_38 (and_38_out, SP, T0, INX, Set_CLK);
  and and_39 (LIDS_SP[1], SP, T0, DCX, Enable_CLK);
  and and_40 (and_40_out, SP, T0, DCX, Set_CLK);
  and and_41 (and_41_out, SP, T0, LDAX_16, Enable_CLK);
  and and_42 (and_42_out, SP, T0, LDAX_16, Set_CLK);
  and and_43 (and_43_out, SP, T0, STAX_16, Enable_CLK);
  and and_44 (and_44_out, SP, T0, STAX_16, Set_CLK);
  and and_45 (LIDS_PC[3], PC, T0, LXI, Enable_CLK);
  and and_46 (and_46_out, PC, T0, LXI, Set_CLK);
  and and_47 (and_47_out, PC, T0, LDAX, Enable_CLK);
  and and_48 (and_48_out, PC, T0, LDAX, Set_CLK);
  and and_49 (and_49_out, PC, T0, STAX, Enable_CLK);
  and and_50 (and_50_out, PC, T0, STAX, Set_CLK);
  and and_51 (LIDS_PC[2], PC, T0, INX, Enable_CLK);
  and and_52 (and_52_out, PC, T0, INX, Set_CLK);
  and and_53 (LIDS_PC[1], PC, T0, DCX, Enable_CLK);
  and and_54 (and_54_out, PC, T0, DCX, Set_CLK);
  or or_1 (CLK_PSW, and_2_out, and_8_out, and_10_out);
  or or_2 (LIDS_PSW[0], and_3_out, and_5_out);
  or or_3 (CLK_BC, and_12_out, and_18_out, and_20_out);
  or or_4 (LIDS_BC[0], and_13_out, and_15_out);
  or or_5 (CLK_DE, and_22_out, and_28_out, and_30_out);
  or or_6 (LIDS_DE[0], and_23_out, and_25_out);
  or or_7 (or_7_out, LIDS_SP[3], and_41_out, and_43_out);
  or or_8 (CLK_SP, and_32_out, and_38_out, and_40_out);
  or or_9 (LIDS_SP[0], and_33_out, and_35_out);
  or or_10 (or_10_out, and_33_out, and_41_out);
  or or_11 (or_11_out, and_35_out, and_43_out);
  or or_12 (or_12_out, and_36_out, and_44_out);
  or or_13 (or_13_out, and_33_out, and_41_out);
  or or_14 (or_14_out, and_34_out, and_42_out);
  or or_15 (or_15_out, and_35_out, and_43_out);
  or or_16 (CLK_PC, and_46_out, and_52_out, and_54_out);
  or or_17 (LIDS_PC[0], and_47_out, and_49_out);
  or or_18 (Show_16, LIDS_PSW[3], LIDS_BC[3], LIDS_DE[3], or_7_out, LIDS_PC[3]);
  or or_19 (Show_M, and_3_out, and_13_out, and_23_out, or_10_out, and_47_out);
  or or_20 (Enable_M, and_5_out, and_15_out, and_25_out, or_11_out, and_49_out);
  or or_21 (Set_M, and_6_out, and_16_out, and_26_out, or_12_out, and_50_out);
  or or_22 (LIDS_A[3], and_3_out, and_13_out, and_23_out, or_13_out, and_47_out);
  or or_23 (CLK_A, and_4_out, and_14_out, and_24_out, or_14_out, and_48_out);
  or or_24 (LIDS_A[0], and_5_out, and_15_out, and_25_out, or_15_out, and_49_out);

  assign LIDS_A[2:1] = 2'b00;
endmodule

module ALU_Signal (
  input  Enable_CLK,
  input  Set_CLK,
  input  T0,
  input  [2:0] S,
  input  Rs_B,
  input  Rs_C,
  input  Rs_D,
  input  Rs_E,
  input  Rs_M,
  input  Rs_8,
  output [2:0] S_2,
  output [3:0] LIDS_B,
  output [3:0] LIDS_C,
  output [3:0] LIDS_D,
  output [3:0] LIDS_E,
  output Show_M,
  output Show_8,
  output [3:0] LIDS_DE,
  output LD_ACC,
  output CLK_ACC
);

  wire and_2_out, and_4_out, and_6_out, and_8_out, and_10_out, and_12_out;

  and and_1 (LIDS_B[0], Rs_B, T0, Enable_CLK);
  and and_2 (and_2_out, Rs_B, T0, Set_CLK);
  and and_3 (LIDS_C[0], Rs_C, T0, Enable_CLK);
  and and_4 (and_4_out, Rs_C, T0, Set_CLK);
  and and_5 (LIDS_D[0], Rs_D, T0, Enable_CLK);
  and and_6 (and_6_out, Rs_D, T0, Set_CLK);
  and and_7 (LIDS_E[0], Rs_E, T0, Enable_CLK);
  and and_8 (and_8_out, Rs_E, T0, Set_CLK);
  and and_9 (LIDS_DE[0], Rs_M, T0, Enable_CLK);
  and and_10 (and_10_out, Rs_M, T0, Set_CLK);
  and and_11 (Show_8, Rs_8, T0, Enable_CLK);
  and and_12 (and_12_out, Rs_8, T0, Set_CLK);
  or or_1 (CLK_ACC, and_2_out, and_4_out, and_6_out, and_8_out, and_10_out, and_12_out);
  or or_2 (LD_ACC, LIDS_B[0], LIDS_C[0], LIDS_D[0], LIDS_E[0], LIDS_DE[0], Show_8);

  assign LIDS_B[3:1] = 3'b000;
  assign LIDS_C[3:1] = 3'b000;
  assign LIDS_D[3:1] = 3'b000;
  assign LIDS_DE[3:1] = 3'b000;
  assign LIDS_E[3:1] = 3'b000;
  assign S_2 = S;
  assign Show_M = LIDS_DE[0];
endmodule

module Others_Signal (
  input  Enable_CLK,
  input  Set_CLK,
  input  T0,
  input  T1,
  input  T2,
  input  T3,
  input  T4,
  input  JMP,
  input  CALL,
  input  RET,
  input  DI,
  input  EI,
  input  OUT,
  input  IN,
  output Show_16,
  output CLK_PC,
  output CLK_DE,
  output CLK_SP,
  output Enable_M,
  output Set_M,
  output CLK_E,
  output CLK_D,
  output IEN_0,
  output IEN_1,
  output IEN_CLK,
  output LD_OUT,
  output CLK_OUT,
  output Show_IN,
  output CLK_A,
  output [3:0] LIDS_A,
  output [3:0] LIDS_D,
  output [3:0] LIDS_E,
  output [3:0] LIDS_DE,
  output [3:0] LIDS_PC,
  output [3:0] LIDS_SP
);

  wire and_2_out, and_4_out, and_9_out, and_10_out, and_14_out, and_15_out, and_16_out, and_18_out,
       and_19_out, and_20_out, and_23_out, and_24_out, and_28_out;

  and and_1 (IEN_0, DI, T0, Enable_CLK);
  and and_2 (and_2_out, DI, T0, Set_CLK);
  and and_3 (IEN_1, EI, T0, Enable_CLK);
  and and_4 (and_4_out, EI, T0, Set_CLK);
  and and_5 (LD_OUT, OUT, T0, Enable_CLK);
  and and_6 (CLK_OUT, OUT, T0, Set_CLK);
  and and_7 (LIDS_A[3], IN, T0, Enable_CLK);
  and and_8 (CLK_A, IN, T0, Set_CLK);
  and and_9 (and_9_out, JMP, T0, Enable_CLK);
  and and_10 (and_10_out, JMP, T0, Set_CLK);
  and and_11 (LIDS_DE[3], CALL, T0, Enable_CLK);
  and and_12 (CLK_DE, CALL, T0, Set_CLK);
  and and_13 (LIDS_D[0], CALL, T1, Enable_CLK);
  and and_14 (and_14_out, CALL, T1, Set_CLK);
  and and_15 (and_15_out, CALL, T2, Enable_CLK);
  and and_16 (and_16_out, CALL, T2, Set_CLK);
  and and_17 (LIDS_E[0], CALL, T3, Enable_CLK);
  and and_18 (and_18_out, CALL, T3, Set_CLK);
  and and_19 (and_19_out, CALL, T4, Enable_CLK);
  and and_20 (and_20_out, CALL, T4, Set_CLK);
  and and_21 (LIDS_E[3], RET, T0, Enable_CLK);
  and and_22 (CLK_E, RET, T0, Set_CLK);
  and and_23 (and_23_out, RET, T1, Enable_CLK);
  and and_24 (and_24_out, RET, T1, Set_CLK);
  and and_25 (LIDS_D[3], RET, T2, Enable_CLK);
  and and_26 (CLK_D, RET, T2, Set_CLK);
  and and_27 (LIDS_DE[0], RET, T3, Enable_CLK);
  and and_28 (and_28_out, RET, T3, Set_CLK);
  or or_1 (IEN_CLK, and_2_out, and_4_out);
  or or_2 (Show_16, and_9_out, and_19_out);
  or or_3 (LIDS_PC[3], and_9_out, and_19_out, LIDS_DE[0]);
  or or_4 (CLK_PC, and_10_out, and_20_out, and_28_out);
  or or_5 (LIDS_SP[1], LIDS_DE[3], and_15_out);
  or or_6 (LIDS_SP[2], and_23_out, LIDS_DE[0]);
  or or_7 (CLK_SP, CLK_DE, and_16_out, and_24_out, and_28_out);
  or or_8 (LIDS_SP[0], LIDS_D[0], LIDS_E[0], LIDS_E[3], LIDS_D[3]);
  or or_9 (Enable_M, LIDS_D[0], LIDS_E[0], LIDS_E[3], LIDS_D[3]);
  or or_10 (Set_M, and_14_out, and_18_out);

  assign LIDS_A[2:0] = {2'b00, LD_OUT};
  assign LIDS_D[2:1] = 2'b00;
  assign LIDS_DE[2:1] = 2'b00;
  assign LIDS_E[2:1] = 2'b00;
  assign LIDS_PC[2:0] = {2'b00, LIDS_DE[3]};
  assign LIDS_SP[3] = 1'b0;
  assign Show_IN = LIDS_A[3];
endmodule

module Push_Pop (
  input  Enable_CLK,
  input  Set_CLK,
  input  T0,
  input  T1,
  input  T2,
  input  T3,
  input  Push,
  input  PSW,
  input  BC,
  input  DE,
  input  Pop,
  output CLK_Low,
  output [3:0] LIDS_A,
  output [3:0] LIDS_Flags,
  output [3:0] LIDS_B,
  output CLK_High,
  output [3:0] LIDS_C,
  output [3:0] LIDS_D,
  output [3:0] LIDS_E,
  output CLK_SP,
  output Enable_M,
  output Show_M,
  output Set_M,
  output [3:0] LIDS_SP
);

  wire and_1_out, and_2_out, and_3_out, and_4_out, and_5_out, and_6_out, and_7_out, and_8_out, and_9_out,
       and_11_out, and_12_out, and_13_out, and_15_out, and_16_out;

  and and_1 (and_1_out, Push, T0, Enable_CLK);
  and and_2 (and_2_out, Push, T0, Set_CLK);
  and and_3 (and_3_out, Push, T1, Enable_CLK);
  and and_4 (and_4_out, Push, T1, Set_CLK);
  and and_5 (and_5_out, Push, T2, Enable_CLK);
  and and_6 (and_6_out, Push, T2, Set_CLK);
  and and_7 (and_7_out, Push, T3, Enable_CLK);
  and and_8 (and_8_out, Push, T3, Set_CLK);
  and and_9 (and_9_out, Pop, T0, Enable_CLK);
  and and_10 (CLK_Low, Pop, T0, Set_CLK);
  and and_11 (and_11_out, Pop, T1, Enable_CLK);
  and and_12 (and_12_out, Pop, T2, Set_CLK);
  and and_13 (and_13_out, Pop, T2, Enable_CLK);
  and and_14 (CLK_High, Pop, T0, Set_CLK);
  and and_15 (and_15_out, Pop, T3, Enable_CLK);
  and and_16 (and_16_out, Pop, T3, Set_CLK);
  or or_1 (LIDS_SP[1], and_1_out, and_5_out);
  or or_2 (LIDS_SP[2], and_11_out, and_15_out);
  or or_3 (CLK_SP, and_2_out, and_6_out, and_12_out, and_16_out);
  or or_4 (LIDS_SP[0], and_3_out, and_7_out, and_9_out, and_13_out);
  or or_5 (Enable_M, and_3_out, and_7_out);
  or or_6 (Show_M, and_9_out, and_13_out);
  or or_7 (Set_M, and_4_out, and_8_out);
  and and_17 (LIDS_Flags[0], PSW, and_7_out);
  and and_18 (LIDS_A[0], PSW, and_3_out);
  and and_19 (LIDS_Flags[3], PSW, and_9_out);
  and and_20 (LIDS_A[3], PSW, and_13_out);
  and and_21 (LIDS_C[0], BC, and_7_out);
  and and_22 (LIDS_B[0], BC, and_3_out);
  and and_23 (LIDS_C[3], BC, and_9_out);
  and and_24 (LIDS_B[3], BC, and_13_out);
  and and_25 (LIDS_E[0], DE, and_7_out);
  and and_26 (LIDS_D[0], DE, and_3_out);
  and and_27 (LIDS_E[3], DE, and_9_out);
  and and_28 (LIDS_D[3], DE, and_13_out);

  assign LIDS_A[2:1] = 2'b00;
  assign LIDS_B[2:1] = 2'b00;
  assign LIDS_C[2:1] = 2'b00;
  assign LIDS_D[2:1] = 2'b00;
  assign LIDS_E[2:1] = 2'b00;
  assign LIDS_Flags[2:1] = 2'b00;
  assign LIDS_SP[3] = 1'b0;
endmodule

module LIDS_converter (
  input  INR_PC,
  input  SW_PC,
  input  Show_M,
  input  CLK_PC,
  input  CLK_A,
  input  CLK_B,
  input  CLK_C,
  input  CLK_D,
  input  CLK_E,
  input  Enable_M,
  input  Set_M,
  input  Show_8,
  input  Show_M_2,
  input  [3:0] LIDS_DE,
  input  [3:0] LIDS_A,
  input  [3:0] LIDS_B,
  input  [3:0] LIDS_C,
  input  [3:0] LIDS_D,
  input  [3:0] LIDS_E,
  input  CLK_Low,
  input  CLK_High,
  input  CLK_SP,
  input  [3:0] LIDS_A_2,
  input  [3:0] LIDS_Flags,
  input  [3:0] LIDS_B_2,
  input  [3:0] LIDS_C_2,
  input  [3:0] LIDS_D_2,
  input  [3:0] LIDS_E_2,
  input  [3:0] LIDS_SP,
  input  Enable_M_2,
  input  Set_M_2,
  input  Show_M_3,
  input  CLK_PSW,
  input  CLK_BC,
  input  CLK_DE,
  input  CLK_SP_2,
  input  CLK_PC_2,
  input  CLK_A_2,
  input  [3:0] LIDS_PSW,
  input  [3:0] LIDS_BC,
  input  [3:0] LIDS_DE_2,
  input  [3:0] LIDS_SP_2,
  input  [3:0] LIDS_PC,
  input  [3:0] LIDS_A_3,
  input  Show_16,
  input  Show_M_4,
  input  Enable_M_3,
  input  Set_M_3,
  input  [2:0] S,
  input  [3:0] LIDS_B_3,
  input  [3:0] LIDS_C_3,
  input  [3:0] LIDS_D_3,
  input  [3:0] LIDS_E_3,
  input  [3:0] LIDS_DE_3,
  input  Show_M_5,
  input  Show_8_2,
  input  LD_ACC,
  input  CLK_ACC,
  input  CLK_A_3,
  input  CLK_D_2,
  input  CLK_E_2,
  input  CLK_DE_2,
  input  CLK_PC_3,
  input  CLK_SP_3,
  input  Enable_M_4,
  input  Set_M_4,
  input  IEN_0,
  input  IEN_1,
  input  CLK_IEN,
  input  LD_OUT,
  input  CLK_OUT,
  input  Show_IN,
  input  Show_16_2,
  input  [3:0] LIDS_A_4,
  input  [3:0] LIDS_D_4,
  input  [3:0] LIDS_E_4,
  input  [3:0] LIDS_DE_4,
  input  [3:0] LIDS_PC_2,
  input  [3:0] LIDS_SP_3,
  output [10:0] CLK_PULSES,
  output [23:0] LIDS_8BIT,
  output [19:0] LIDS_16BIT,
  output [2:0] EnStSw_M,
  output Show_8_3,
  output Show_16_3,
  output Pass_ACC,
  output [2:0] S_2,
  output IEN_0_2,
  output IEN_1_2,
  output CLK_IEN_2,
  output LD_OUT_2,
  output CLK_OUT_2,
  output Show_IN_2
);

  or or_1 (CLK_PULSES[10], CLK_A, CLK_High, CLK_A_2, CLK_ACC, CLK_A_3);
  or or_2 (CLK_PULSES[8], CLK_B, CLK_High);
  or or_3 (CLK_PULSES[7], CLK_C, CLK_Low);
  or or_4 (CLK_PULSES[6], CLK_D, CLK_High, CLK_D_2);
  or or_5 (CLK_PULSES[5], CLK_E, CLK_Low, CLK_E_2);
  or or_6 (CLK_PULSES[2], CLK_DE, CLK_DE_2);
  or or_7 (CLK_PULSES[1], CLK_PC, CLK_PC_2, CLK_PC_3);
  or or_8 (CLK_PULSES[0], CLK_SP, CLK_SP_2, CLK_SP_3);
  // Probe on LIDS_8BIT[23:20]
  assign LIDS_8BIT[23:20] = LIDS_A | LIDS_A_2 | {LD_ACC, 3'b000} | LIDS_A_3 | LIDS_A_4;  // OR_Gate or_9, 4 bits wide
  // Probe on LIDS_Flags
  assign LIDS_8BIT[15:12] = LIDS_B | LIDS_B_2 | LIDS_B_3;  // OR_Gate or_10, 4 bits wide
  // Probe on LIDS_8BIT[15:12]
  // Probe on LIDS_8BIT[11:8]
  assign LIDS_8BIT[11:8] = LIDS_C | LIDS_C_3 | LIDS_C_2;  // OR_Gate or_11, 4 bits wide
  assign LIDS_8BIT[7:4] = LIDS_D | LIDS_D_2 | LIDS_D_3 | LIDS_D_4;  // OR_Gate or_12, 4 bits wide
  // Probe on LIDS_8BIT[7:4]
  assign LIDS_8BIT[3:0] = LIDS_E | LIDS_E_2 | LIDS_E_3 | LIDS_E_4;  // OR_Gate or_13, 4 bits wide
  // Probe on LIDS_8BIT[3:0]
  assign LIDS_16BIT[11:8] = LIDS_DE | LIDS_DE_2 | LIDS_DE_3 | LIDS_DE_4;  // OR_Gate or_14, 4 bits wide
  assign LIDS_16BIT[7:4] = {1'b0, INR_PC, 1'b0, SW_PC} | LIDS_PC | LIDS_PC_2;  // OR_Gate or_15, 4 bits wide
  assign LIDS_16BIT[3:0] = LIDS_SP | LIDS_SP_2 | LIDS_SP_3;  // OR_Gate or_16, 4 bits wide
  or or_17 (EnStSw_M[2], Enable_M, Enable_M_2, Enable_M_3, Enable_M_4);
  or or_18 (EnStSw_M[1], Set_M, Set_M_2, Set_M_3, Set_M_4);
  or or_19 (EnStSw_M[0], Show_M, Show_M_2, Show_M_3, Show_M_4, Show_M_5);
  or or_20 (Show_8_3, Show_8, Show_8_2);
  or or_21 (Show_16_3, Show_16, Show_16_2);
  // Probe on CLK_PULSES[10]
  // Probe on CLK_Low
  // Probe on CLK_PULSES[8]
  // Probe on CLK_PULSES[7]
  // Probe on CLK_PULSES[6]
  // Probe on CLK_PULSES[5]
  // Probe on CLK_PSW
  // Probe on CLK_BC
  // Probe on CLK_PULSES[2]
  // Probe on CLK_PULSES[1]
  // Probe on CLK_PULSES[0]
  // Probe on LIDS_PSW
  // Probe on LIDS_BC
  // Probe on LIDS_16BIT[11:8]
  // Probe on LIDS_16BIT[7:4]
  // Probe on LIDS_16BIT[3:0]
  // Probe on EnStSw_M[2]
  // Probe on EnStSw_M[1]
  // Probe on EnStSw_M[0]

  assign CLK_IEN_2 = CLK_IEN;
  assign CLK_OUT_2 = CLK_OUT;
  assign {CLK_PULSES[9], CLK_PULSES[4:3]} = {CLK_Low, CLK_PSW, CLK_BC};
  assign IEN_0_2 = IEN_0;
  assign IEN_1_2 = IEN_1;
  assign LD_OUT_2 = LD_OUT;
  assign LIDS_8BIT[19:16] = LIDS_Flags;
  assign LIDS_16BIT[19:12] = {LIDS_PSW, LIDS_BC};
  assign Pass_ACC = LD_ACC;
  assign S_2 = S;
  assign Show_IN_2 = Show_IN;
endmodule

module SIPO_Shift_Reg (
  input  [7:0] _8bit_Bus_IN,
  input  _1bit_Instruction_IN,
  input  Enable,
  input  Shift__1,
  input  CLR,
  output [23:0] _24bit_Out,
  output [2:0] _3bit_Out
);

  Register register_1 (.D(_24bit_Out[7:0]), .en(Enable), .Q(_24bit_Out[15:8]), .clk(Shift__1), .clr(CLR));
  Register register_2 (.D(_8bit_Bus_IN), .en(Enable), .Q(_24bit_Out[7:0]), .clk(Shift__1), .clr(CLR));
  Register register_3 (.D(_24bit_Out[15:8]), .en(Enable), .Q(_24bit_Out[23:16]), .clk(Shift__1), .clr(CLR));
  Register #(.width(1)) register_4 (.D(_1bit_Instruction_IN), .en(Enable), .Q(_3bit_Out[0]), .clk(Shift__1), .clr(CLR));
  Register #(.width(1)) register_5 (.D(_3bit_Out[0]), .en(Enable), .Q(_3bit_Out[1]), .clk(Shift__1), .clr(CLR));
  Register #(.width(1)) register_6 (.D(_3bit_Out[1]), .en(Enable), .Q(_3bit_Out[2]), .clk(Shift__1), .clr(CLR));
endmodule

module New_Stepper (
  input  Enable,
  input  CLK,
  input  Reset,
  output Step_1,
  output Step_2,
  output Step_3,
  output Step_4,
  output Step_5,
  output Step_6,
  output Step_7,
  output Step_8,
  output Step_9,
  output Step_10
);

  wire decoder_1_out10, or_1_out;
  wire [3:0] counter_1_q;

  Counter #(.width(4), .max('hf)) counter_1 (
    .count(Enable), .Q(counter_1_q), .clk(CLK), .clr(or_1_out));  // open: load, D, carry
  or or_1 (or_1_out, Reset, decoder_1_out10);
  Decoder #(.select(4), .enable("false")) decoder_1 (
    .out0(Step_1), .out1(Step_2), .out2(Step_3), .out3(Step_4), .out4(Step_5), .out5(Step_6), .out6(Step_7),
    .out7(Step_8), .out8(Step_9), .out9(Step_10), .out10(decoder_1_out10), .sel(counter_1_q));  // open: out11, out12, out13, out14, out15
endmodule

module _3rd_Instr_Fetcher (
  input  Enable_CLK,
  input  Set_CLK,
  input  T0,
  input  T1,
  input  T2,
  input  T3,
  input  T9,
  input  isINSTRUCTION,
  output SW_PC,
  output Show_M,
  output _24bit_Load,
  output Reg_Shift__1,
  output INR_PC,
  output CLK_PC,
  output Decode_Instruction,
  output Reset_SC
);

  wire not_1_out;

  not not_1 (not_1_out, isINSTRUCTION);
  and and_1 (Show_M, T0, Enable_CLK);
  and and_2 (_24bit_Load, T0, Set_CLK);
  and and_3 (INR_PC, T1, isINSTRUCTION, Enable_CLK);
  and and_4 (CLK_PC, T1, isINSTRUCTION, Set_CLK);
  and and_5 (Decode_Instruction, T2, isINSTRUCTION, Set_CLK);
  and and_6 (Reset_SC, T2, not_1_out, Set_CLK);

  assign Reg_Shift__1 = _24bit_Load;
  assign SW_PC = Show_M;
endmodule
